// Logisim project calculator.circ as structural Verilog: 12 circuits, main circuit interface
module \interface  (
  input  in_1,
  input  in_2,
  input  in_3,
  input  Input_B_Display,
  input  in_5,
  input  in_6,
  input  in_7,
  input  in_8,
  input  in_9,
  input  in_10,
  input  in_11,
  input  Input_B,
  input  in_13,
  input  in_14,
  input  in_15,
  input  in_16,
  input  in_17,
  input  in_18,
  input  in_19,
  input  Input_A,
  input  in_21,
  input  in_22,
  input  in_23,
  input  in_24
);

  wire button_5_out, button_7_out, button_8_out, button_12_out, button_13_out, button_14_out,
       custom_register_1_o_1, custom_register_1_o_2, custom_register_1_o_3, custom_register_1_o_4,
       custom_register_1_o_5, custom_register_1_o_6, custom_register_1_o_7, custom_register_1_o_8,
       custom_register_2_o_1, custom_register_2_o_2, custom_register_2_o_3, custom_register_2_o_4,
       custom_register_2_o_5, custom_register_2_o_6, custom_register_2_o_7, custom_register_2_o_8,
       j_k_ff_1_q, j_k_ff_1_qn, j_k_ff_2_q, j_k_ff_2_qn, or_1_out, or_2_out, or_3_out, or_4_out, or_5_out,
       or_6_out, or_7_out, or_8_out, or_25_out, or_26_out, or_27_out, or_28_out, or_29_out, or_30_out,
       or_31_out, or_32_out;
  wire [2:0] button_11_out;
  wire [7:0] and_8_out, and_16_out, and_24_out, and_32_out, calculator_adder_and_subtractor_1_o_1, or_16_out,
       or_24_out, two_complement_1_out_one, two_complement_2_out_one, two_complement_3_out_one,
       two_complement_4_out_one;
  wire [8:0] pos_neg_output_1_pos_or_neg;

  Button button_1 ();  // open: out
  LED led_1 ();  // open: in
  LED led_2 ();  // open: in
  Button button_2 ();  // open: out
  Button button_3 ();  // open: out
  Button button_4 ();  // open: out
  and and_1 (and_8_out[7], custom_register_1_o_8, j_k_ff_1_qn);
  and and_2 (and_8_out[6], custom_register_1_o_7, j_k_ff_1_qn);
  LED led_3 ();  // open: in
  and and_3 (and_8_out[5], custom_register_1_o_6, j_k_ff_1_qn);
  and and_4 (and_8_out[4], custom_register_1_o_5, j_k_ff_1_qn);
  LED led_4 ();  // open: in
  LED led_5 ();  // open: in
  and and_5 (and_8_out[3], custom_register_1_o_4, j_k_ff_1_qn);
  and and_6 (and_8_out[2], custom_register_1_o_3, j_k_ff_1_qn);
  LED led_6 (.in(j_k_ff_1_q));
  LED led_7 ();  // open: in
  LED led_8 ();  // open: in
  and and_7 (and_8_out[1], custom_register_1_o_2, j_k_ff_1_qn);
  and and_8 (and_8_out[0], custom_register_1_o_1, j_k_ff_1_qn);
  or or_1 (or_1_out, and_8_out[7], two_complement_2_out_one[7]);
  LED led_9 (.in(or_1_out));
  LED led_10 ();  // open: in
  LED led_11 ();  // open: in
  or or_2 (or_2_out, and_8_out[6], two_complement_2_out_one[6]);
  LED led_12 (.in(or_2_out));
  LED led_13 ();  // open: in
  LED led_14 ();  // open: in
  LED led_15 ();  // open: in
  Button button_5 (.out(button_5_out));
  J_K_Flip_Flop j_k_ff_1 (
    .J(1'b1), .K(1'b1), .clk(button_5_out), .Q(j_k_ff_1_q), .Qn(j_k_ff_1_qn));  // open: preset, reset
  or or_3 (or_3_out, and_8_out[5], two_complement_2_out_one[5]);
  LED led_16 (.in(or_3_out));
  Button button_6 ();  // open: out
  LED led_17 ();  // open: in
  LED led_18 ();  // open: in
  LED led_19 ();  // open: in
  LED led_20 (.in(j_k_ff_1_q));
  or or_4 (or_4_out, and_8_out[4], two_complement_2_out_one[4]);
  LED led_21 (.in(or_4_out));
  LED led_22 ();  // open: in
  LED led_23 ();  // open: in
  or or_5 (or_5_out, and_8_out[3], two_complement_2_out_one[3]);
  or or_6 (or_6_out, and_8_out[2], two_complement_2_out_one[2]);
  LED led_24 (.in(or_5_out));
  LED led_25 (.in(or_6_out));
  LED led_26 ();  // open: in
  LED led_27 ();  // open: in
  LED led_28 ();  // open: in
  and and_9 (and_16_out[7], j_k_ff_1_q, custom_register_1_o_8);
  or or_7 (or_7_out, and_8_out[1], two_complement_2_out_one[1]);
  LED led_29 (.in(or_7_out));
  LED led_30 ();  // open: in
  LED led_31 ();  // open: in
  LED led_32 ();  // open: in
  Button button_7 (.out(button_7_out));
  Button button_8 (.out(button_8_out));
  and and_10 (and_16_out[6], j_k_ff_1_q, custom_register_1_o_7);
  and and_11 (and_16_out[5], j_k_ff_1_q, custom_register_1_o_6);
  or or_8 (or_8_out, and_8_out[0], two_complement_2_out_one[0]);
  LED led_33 (.in(or_8_out));
  LED led_34 ();  // open: in
  LED led_35 ();  // open: in
  and and_12 (and_16_out[3], j_k_ff_1_q, custom_register_1_o_4);
  and and_13 (and_16_out[4], j_k_ff_1_q, custom_register_1_o_5);
  LED led_36 ();  // open: in
  and and_14 (and_16_out[2], j_k_ff_1_q, custom_register_1_o_3);
  and and_15 (and_16_out[1], j_k_ff_1_q, custom_register_1_o_2);
  LED led_37 ();  // open: in
  Custom_Register custom_register_1 (
    .i_1(in_24), .i_2(in_23), .i_3(in_22), .i_4(in_21), .i_5(Input_A), .i_6(in_19), .i_7(in_18), .i_8(in_17),
    .Clock(button_7_out), .Reset(button_8_out), .O_1(custom_register_1_o_1), .O_2(custom_register_1_o_2),
    .O_3(custom_register_1_o_3), .O_4(custom_register_1_o_4), .O_5(custom_register_1_o_5),
    .O_6(custom_register_1_o_6), .O_7(custom_register_1_o_7), .O_8(custom_register_1_o_8));
  and and_16 (and_16_out[0], j_k_ff_1_q, custom_register_1_o_1);
  Two_Complement two_complement_1 (
    .Eight(and_16_out[7]), .Seven(and_16_out[6]), .Six(and_16_out[5]), .Five(and_16_out[4]),
    .Four(and_16_out[3]), .Three(and_16_out[2]), .Two(and_16_out[1]), .One(and_16_out[0]), .Toggle(1'b1),
    .Out_One(two_complement_1_out_one[0]), .Out_Two(two_complement_1_out_one[1]),
    .Out_Three(two_complement_1_out_one[2]), .Out_Four(two_complement_1_out_one[3]),
    .Out_Five(two_complement_1_out_one[4]), .Out_Six(two_complement_1_out_one[5]),
    .Out_Seven(two_complement_1_out_one[6]), .Out_Eight(two_complement_1_out_one[7]));  // open: Pos_or_Neg
  Two_Complement two_complement_2 (
    .Eight(two_complement_1_out_one[7]), .Seven(two_complement_1_out_one[6]),
    .Six(two_complement_1_out_one[5]), .Five(two_complement_1_out_one[4]),
    .Four(two_complement_1_out_one[3]), .Three(two_complement_1_out_one[2]),
    .Two(two_complement_1_out_one[1]), .One(two_complement_1_out_one[0]), .Toggle(1'b1),
    .Out_One(two_complement_2_out_one[0]), .Out_Two(two_complement_2_out_one[1]),
    .Out_Three(two_complement_2_out_one[2]), .Out_Four(two_complement_2_out_one[3]),
    .Out_Five(two_complement_2_out_one[4]), .Out_Six(two_complement_2_out_one[5]),
    .Out_Seven(two_complement_2_out_one[6]), .Out_Eight(two_complement_2_out_one[7]));  // open: Pos_or_Neg
  or or_9 (or_16_out[7], and_8_out[7], two_complement_1_out_one[7]);
  or or_10 (or_16_out[6], and_8_out[6], two_complement_1_out_one[6]);
  or or_11 (or_16_out[5], and_8_out[5], two_complement_1_out_one[5]);
  LED led_38 (.in(pos_neg_output_1_pos_or_neg[0]));
  or or_12 (or_16_out[4], and_8_out[4], two_complement_1_out_one[4]);
  or or_13 (or_16_out[3], and_8_out[3], two_complement_1_out_one[3]);
  LED led_39 (.in(pos_neg_output_1_pos_or_neg[1]));
  or or_14 (or_16_out[2], and_8_out[2], two_complement_1_out_one[2]);
  LED led_40 (.in(pos_neg_output_1_pos_or_neg[2]));
  or or_15 (or_16_out[1], and_8_out[1], two_complement_1_out_one[1]);
  LED led_41 (.in(pos_neg_output_1_pos_or_neg[3]));
  Button button_9 (.out(button_11_out[2]));
  or or_16 (or_16_out[0], and_8_out[0], two_complement_1_out_one[0]);
  LED led_42 (.in(pos_neg_output_1_pos_or_neg[4]));
  Button button_10 (.out(button_11_out[1]));
  Button button_11 (.out(button_11_out[0]));
  LED led_43 (.in(pos_neg_output_1_pos_or_neg[5]));
  or or_17 (or_24_out[7], two_complement_3_out_one[7], and_24_out[7]);
  LED led_44 (.in(pos_neg_output_1_pos_or_neg[6]));
  or or_18 (or_24_out[6], two_complement_3_out_one[6], and_24_out[6]);
  LED led_45 (.in(pos_neg_output_1_pos_or_neg[7]));
  or or_19 (or_24_out[5], two_complement_3_out_one[5], and_24_out[5]);
  Calculator_Adder_and_Subtractor calculator_adder_and_subtractor_1 (
    .A_8(or_16_out[7]), .A_7(or_16_out[6]), .A_6(or_16_out[5]), .A_5(or_16_out[4]), .A_4(or_16_out[3]),
    .A_3(or_16_out[2]), .A_2(or_16_out[1]), .A_1(or_16_out[0]), .B_8(or_24_out[7]), .B_7(or_24_out[6]),
    .B_6(or_24_out[5]), .B_5(or_24_out[4]), .B_4(or_24_out[3]), .B_3(or_24_out[2]), .B_2(or_24_out[1]),
    .B_1(or_24_out[0]), .Reset(button_11_out[0]), .Add(button_11_out[1]), .Subtract(button_11_out[2]),
    .O_8(calculator_adder_and_subtractor_1_o_1[7]), .O_7(calculator_adder_and_subtractor_1_o_1[6]),
    .O_6(calculator_adder_and_subtractor_1_o_1[5]), .O_5(calculator_adder_and_subtractor_1_o_1[4]),
    .O_4(calculator_adder_and_subtractor_1_o_1[3]), .O_3(calculator_adder_and_subtractor_1_o_1[2]),
    .O_2(calculator_adder_and_subtractor_1_o_1[1]), .O_1(calculator_adder_and_subtractor_1_o_1[0]));
  Pos_Neg_Output pos_neg_output_1 (
    .i_8(calculator_adder_and_subtractor_1_o_1[7]), .i_7(calculator_adder_and_subtractor_1_o_1[6]),
    .i_6(calculator_adder_and_subtractor_1_o_1[5]), .i_5(calculator_adder_and_subtractor_1_o_1[4]),
    .i_4(calculator_adder_and_subtractor_1_o_1[3]), .i_3(calculator_adder_and_subtractor_1_o_1[2]),
    .i_2(calculator_adder_and_subtractor_1_o_1[1]), .i_1(calculator_adder_and_subtractor_1_o_1[0]),
    .O_8(pos_neg_output_1_pos_or_neg[8]), .O_7(pos_neg_output_1_pos_or_neg[7]),
    .O_6(pos_neg_output_1_pos_or_neg[6]), .O_5(pos_neg_output_1_pos_or_neg[5]),
    .O_4(pos_neg_output_1_pos_or_neg[4]), .O_3(pos_neg_output_1_pos_or_neg[3]),
    .O_2(pos_neg_output_1_pos_or_neg[2]), .O_1(pos_neg_output_1_pos_or_neg[1]),
    .Pos_or_Neg(pos_neg_output_1_pos_or_neg[0]));
  LED led_46 (.in(pos_neg_output_1_pos_or_neg[8]));
  or or_20 (or_24_out[4], two_complement_3_out_one[4], and_24_out[4]);
  or or_21 (or_24_out[3], two_complement_3_out_one[3], and_24_out[3]);
  or or_22 (or_24_out[2], two_complement_3_out_one[2], and_24_out[2]);
  or or_23 (or_24_out[1], two_complement_3_out_one[1], and_24_out[1]);
  or or_24 (or_24_out[0], two_complement_3_out_one[0], and_24_out[0]);
  and and_17 (and_24_out[7], custom_register_2_o_8, j_k_ff_2_qn);
  and and_18 (and_24_out[6], custom_register_2_o_7, j_k_ff_2_qn);
  and and_19 (and_24_out[5], custom_register_2_o_6, j_k_ff_2_qn);
  and and_20 (and_24_out[4], custom_register_2_o_5, j_k_ff_2_qn);
  LED led_47 (.in(j_k_ff_2_q));
  and and_21 (and_24_out[3], custom_register_2_o_4, j_k_ff_2_qn);
  and and_22 (and_24_out[2], custom_register_2_o_3, j_k_ff_2_qn);
  and and_23 (and_24_out[1], custom_register_2_o_2, j_k_ff_2_qn);
  and and_24 (and_24_out[0], custom_register_2_o_1, j_k_ff_2_qn);
  or or_25 (or_25_out, and_24_out[7], two_complement_4_out_one[7]);
  LED led_48 (.in(or_25_out));
  Button button_12 (.out(button_12_out));
  or or_26 (or_26_out, and_24_out[6], two_complement_4_out_one[6]);
  LED led_49 (.in(or_26_out));
  J_K_Flip_Flop j_k_ff_2 (
    .J(1'b1), .K(1'b1), .clk(button_12_out), .Q(j_k_ff_2_q), .Qn(j_k_ff_2_qn));  // open: preset, reset
  or or_27 (or_27_out, and_24_out[5], two_complement_4_out_one[5]);
  or or_28 (or_28_out, and_24_out[4], two_complement_4_out_one[4]);
  LED led_50 (.in(or_27_out));
  LED led_51 (.in(or_28_out));
  LED led_52 (.in(j_k_ff_2_q));
  or or_29 (or_29_out, and_24_out[3], two_complement_4_out_one[3]);
  LED led_53 (.in(or_29_out));
  or or_30 (or_30_out, and_24_out[2], two_complement_4_out_one[2]);
  LED led_54 (.in(or_30_out));
  Button button_13 (.out(button_13_out));
  Button button_14 (.out(button_14_out));
  and and_25 (and_32_out[7], j_k_ff_2_q, custom_register_2_o_8);
  or or_31 (or_31_out, and_24_out[1], two_complement_4_out_one[1]);
  LED led_55 (.in(or_31_out));
  and and_26 (and_32_out[6], j_k_ff_2_q, custom_register_2_o_7);
  and and_27 (and_32_out[5], j_k_ff_2_q, custom_register_2_o_6);
  or or_32 (or_32_out, and_24_out[0], two_complement_4_out_one[0]);
  LED led_56 (.in(or_32_out));
  and and_28 (and_32_out[4], j_k_ff_2_q, custom_register_2_o_5);
  and and_29 (and_32_out[3], j_k_ff_2_q, custom_register_2_o_4);
  and and_30 (and_32_out[2], j_k_ff_2_q, custom_register_2_o_3);
  and and_31 (and_32_out[1], j_k_ff_2_q, custom_register_2_o_2);
  Custom_Register custom_register_2 (
    .i_1(in_16), .i_2(in_15), .i_3(in_14), .i_4(in_13), .i_5(Input_B), .i_6(in_11), .i_7(in_10), .i_8(in_9),
    .Clock(button_13_out), .Reset(button_14_out), .O_1(custom_register_2_o_1), .O_2(custom_register_2_o_2),
    .O_3(custom_register_2_o_3), .O_4(custom_register_2_o_4), .O_5(custom_register_2_o_5),
    .O_6(custom_register_2_o_6), .O_7(custom_register_2_o_7), .O_8(custom_register_2_o_8));
  and and_32 (and_32_out[0], j_k_ff_2_q, custom_register_2_o_1);
  Two_Complement two_complement_3 (
    .Eight(and_32_out[7]), .Seven(and_32_out[6]), .Six(and_32_out[5]), .Five(and_32_out[4]),
    .Four(and_32_out[3]), .Three(and_32_out[2]), .Two(and_32_out[1]), .One(and_32_out[0]), .Toggle(1'b1),
    .Out_One(two_complement_3_out_one[0]), .Out_Two(two_complement_3_out_one[1]),
    .Out_Three(two_complement_3_out_one[2]), .Out_Four(two_complement_3_out_one[3]),
    .Out_Five(two_complement_3_out_one[4]), .Out_Six(two_complement_3_out_one[5]),
    .Out_Seven(two_complement_3_out_one[6]), .Out_Eight(two_complement_3_out_one[7]));  // open: Pos_or_Neg
  Two_Complement two_complement_4 (
    .Eight(two_complement_3_out_one[7]), .Seven(two_complement_3_out_one[6]),
    .Six(two_complement_3_out_one[5]), .Five(two_complement_3_out_one[4]),
    .Four(two_complement_3_out_one[3]), .Three(two_complement_3_out_one[2]),
    .Two(two_complement_3_out_one[1]), .One(two_complement_3_out_one[0]), .Toggle(1'b1),
    .Out_One(two_complement_4_out_one[0]), .Out_Two(two_complement_4_out_one[1]),
    .Out_Three(two_complement_4_out_one[2]), .Out_Four(two_complement_4_out_one[3]),
    .Out_Five(two_complement_4_out_one[4]), .Out_Six(two_complement_4_out_one[5]),
    .Out_Seven(two_complement_4_out_one[6]), .Out_Eight(two_complement_4_out_one[7]));  // open: Pos_or_Neg

  // Notes on the sheet:
  //   +/-
  //   +/-
  //   Load
  //   Subtract
  //   Reset
  //   +/-
  //   Input A Display
  //   +/-
  //   +/-
  //   8 bit Binary Calculator
  //   +/-
  //   +/-
  //   +/-
  //   Output
  //   Load
  //   Reset
  //   Input B
  //   +/-
  //   Subtract
  //   Add
  //   Reset
  //   +/-
  //   +/-
  //   +/-
  //   Load
  //   Reset
endmodule

module Custom_Register (
  input  i_1,
  input  i_2,
  input  i_3,
  input  i_4,
  input  i_5,
  input  i_6,
  input  i_7,
  input  i_8,
  input  Clock,
  input  Reset,
  output O_1,
  output O_2,
  output O_3,
  output O_4,
  output O_5,
  output O_6,
  output O_7,
  output O_8
);

  D_Flip_Flop d_ff_1 (.D(i_1), .clk(Clock), .Q(O_1), .reset(Reset));  // open: Qn, preset
  D_Flip_Flop d_ff_2 (.D(i_2), .clk(Clock), .Q(O_2), .reset(Reset));  // open: Qn, preset
  D_Flip_Flop d_ff_3 (.D(i_3), .clk(Clock), .Q(O_3), .reset(Reset));  // open: Qn, preset
  D_Flip_Flop d_ff_4 (.D(i_4), .clk(Clock), .Q(O_4), .reset(Reset));  // open: Qn, preset
  D_Flip_Flop d_ff_5 (.D(i_5), .clk(Clock), .Q(O_5), .reset(Reset));  // open: Qn, preset
  D_Flip_Flop d_ff_6 (.D(i_6), .clk(Clock), .Q(O_6), .reset(Reset));  // open: Qn, preset
  D_Flip_Flop d_ff_7 (.D(i_7), .clk(Clock), .Q(O_7), .reset(Reset));  // open: Qn, preset
  D_Flip_Flop d_ff_8 (.D(i_8), .clk(Clock), .Q(O_8), .reset(Reset));  // open: Qn, preset
endmodule

module Full_adder (
  input  C_in,
  input  A,
  input  B,
  output Sum,
  output C_out
);

  wire and_1_out, and_2_out, xor_1_out;

  xor xor_1 (xor_1_out, A, B);
  and and_1 (and_1_out, B, A);
  xor xor_2 (Sum, C_in, xor_1_out);
  and and_2 (and_2_out, xor_1_out, C_in);
  or or_1 (C_out, and_2_out, and_1_out);
endmodule

module Half_adder (
  input  A,
  input  B,
  output Sum,
  output C_out
);

  xor xor_1 (Sum, A, B);
  and and_1 (C_out, B, A);
endmodule

module Eight_bit_adder (
  input  A_1,
  input  B_1,
  input  A_2,
  input  B_2,
  input  A_3,
  input  B_3,
  input  A_4,
  input  B_4,
  input  A_5,
  input  B_5,
  input  A_6,
  input  B_6,
  input  A_7,
  input  B_7,
  input  A_8,
  input  B_8,
  output O_1,
  output O_2,
  output O_3,
  output O_4,
  output O_5,
  output O_6,
  output O_7,
  output O_8,
  output Overflow
);

  wire full_adder_1_c_out, full_adder_2_c_out, full_adder_3_c_out, full_adder_4_c_out, full_adder_5_c_out,
       full_adder_6_c_out, full_adder_7_c_out;

  Full_adder full_adder_1 (.A(A_1), .B(B_1), .Sum(O_1), .C_out(full_adder_1_c_out));  // open: C_in
  Full_adder full_adder_2 (.C_in(full_adder_1_c_out), .A(A_2), .B(B_2), .Sum(O_2), .C_out(full_adder_2_c_out));
  Full_adder full_adder_3 (.C_in(full_adder_2_c_out), .A(A_3), .B(B_3), .Sum(O_3), .C_out(full_adder_3_c_out));
  Full_adder full_adder_4 (.C_in(full_adder_3_c_out), .A(A_4), .B(B_4), .Sum(O_4), .C_out(full_adder_4_c_out));
  Full_adder full_adder_5 (.C_in(full_adder_4_c_out), .A(A_5), .B(B_5), .Sum(O_5), .C_out(full_adder_5_c_out));
  Full_adder full_adder_6 (.C_in(full_adder_5_c_out), .A(A_6), .B(B_6), .Sum(O_6), .C_out(full_adder_6_c_out));
  Full_adder full_adder_7 (.C_in(full_adder_6_c_out), .A(A_7), .B(B_7), .Sum(O_7), .C_out(full_adder_7_c_out));
  Full_adder full_adder_8 (.C_in(full_adder_7_c_out), .A(A_8), .B(B_8), .Sum(O_8), .C_out(Overflow));
endmodule

module Calculating_adder (
  input  Reset,
  input  Add,
  input  A_1,
  input  B_1,
  input  A_2,
  input  B_2,
  input  A_3,
  input  B_3,
  input  A_4,
  input  B_4,
  input  A_5,
  input  B_5,
  input  A_6,
  input  B_6,
  input  A_7,
  input  B_7,
  input  A_8,
  input  B_8,
  output O_1,
  output O_2,
  output O_3,
  output O_4,
  output O_5,
  output O_6,
  output O_7,
  output O_8,
  output Overflow
);

  wire eight_bit_adder_1_o_1, eight_bit_adder_1_o_2, eight_bit_adder_1_o_3, eight_bit_adder_1_o_4,
       eight_bit_adder_1_o_5, eight_bit_adder_1_o_6, eight_bit_adder_1_o_7, eight_bit_adder_1_o_8,
       eight_bit_adder_1_overflow;

  Eight_bit_adder eight_bit_adder_1 (
    .A_1(A_1), .B_1(B_1), .A_2(A_2), .B_2(B_2), .A_3(A_3), .B_3(B_3), .A_4(A_4), .B_4(B_4), .A_5(A_5),
    .B_5(B_5), .A_6(A_6), .B_6(B_6), .A_7(A_7), .B_7(B_7), .A_8(A_8), .B_8(B_8), .O_1(eight_bit_adder_1_o_1),
    .O_2(eight_bit_adder_1_o_2), .O_3(eight_bit_adder_1_o_3), .O_4(eight_bit_adder_1_o_4),
    .O_5(eight_bit_adder_1_o_5), .O_6(eight_bit_adder_1_o_6), .O_7(eight_bit_adder_1_o_7),
    .O_8(eight_bit_adder_1_o_8), .Overflow(eight_bit_adder_1_overflow));
  Overflow_Register overflow_register_1 (
    .i_1(eight_bit_adder_1_o_1), .i_2(eight_bit_adder_1_o_2), .i_4(eight_bit_adder_1_o_3),
    .i_5(eight_bit_adder_1_o_4), .i_6(eight_bit_adder_1_o_5), .i_7(eight_bit_adder_1_o_6),
    .i_8(eight_bit_adder_1_o_7), .i_9(eight_bit_adder_1_o_8), .i_10(eight_bit_adder_1_overflow), .Clock(Add),
    .Reset(Reset), .out_12(O_1), .out_13(O_2), .out_14(O_3), .out_15(O_4), .out_16(O_5), .out_17(O_6),
    .out_18(O_7), .out_19(O_8), .out_20(Overflow));
endmodule

module Overflow_Register (
  input  i_1,
  input  i_2,
  input  i_4,
  input  i_5,
  input  i_6,
  input  i_7,
  input  i_8,
  input  i_9,
  input  i_10,
  input  Clock,
  input  Reset,
  output out_12,
  output out_13,
  output out_14,
  output out_15,
  output out_16,
  output out_17,
  output out_18,
  output out_19,
  output out_20
);

  D_Flip_Flop d_ff_1 (.D(i_1), .clk(Clock), .Q(out_12), .reset(Reset));  // open: Qn, preset
  D_Flip_Flop d_ff_2 (.D(i_2), .clk(Clock), .Q(out_13), .reset(Reset));  // open: Qn, preset
  D_Flip_Flop d_ff_3 (.D(i_4), .clk(Clock), .Q(out_14), .reset(Reset));  // open: Qn, preset
  D_Flip_Flop d_ff_4 (.D(i_5), .clk(Clock), .Q(out_15), .reset(Reset));  // open: Qn, preset
  D_Flip_Flop d_ff_5 (.D(i_6), .clk(Clock), .Q(out_16), .reset(Reset));  // open: Qn, preset
  D_Flip_Flop d_ff_6 (.D(i_7), .clk(Clock), .Q(out_17), .reset(Reset));  // open: Qn, preset
  D_Flip_Flop d_ff_7 (.D(i_8), .clk(Clock), .Q(out_18), .reset(Reset));  // open: Qn, preset
  D_Flip_Flop d_ff_8 (.D(i_9), .clk(Clock), .Q(out_19), .reset(Reset));  // open: Qn, preset
  D_Flip_Flop d_ff_9 (.D(i_10), .clk(Clock), .Q(out_20), .reset(Reset));  // open: Qn, preset
endmodule

module draft (
  input  in_1,
  input  in_2,
  input  in_3,
  input  Input_A,
  input  in_5,
  input  in_6,
  input  in_7,
  input  in_8,
  input  in_9,
  input  in_10,
  input  in_11,
  input  in_12,
  input  Input_B,
  input  in_14,
  input  in_15,
  input  in_16,
  input  in_17,
  input  A_8,
  input  A_7,
  input  A_6,
  input  A_5,
  input  A_4,
  input  A_3,
  input  A_2,
  input  A_1,
  input  B_8,
  input  B_7,
  input  B_6,
  input  B_5,
  input  B_4,
  input  B_3,
  input  B_2,
  input  B_1
);

  wire and_25_out, and_34_out, button_1_out, button_2_out, button_3_out, button_4_out, button_5_out,
       button_6_out, button_7_out, button_8_out, clock_1_out, custom_register_2_o_1, custom_register_2_o_2,
       custom_register_2_o_3, custom_register_2_o_4, custom_register_2_o_5, custom_register_2_o_6,
       custom_register_2_o_7, custom_register_2_o_8, custom_register_3_o_1, custom_register_3_o_2,
       custom_register_3_o_3, custom_register_3_o_4, custom_register_3_o_5, custom_register_3_o_6,
       custom_register_3_o_7, custom_register_3_o_8, j_k_ff_1_q, j_k_ff_1_qn, j_k_ff_2_q, j_k_ff_2_qn,
       j_k_ff_3_q, j_k_ff_3_qn, or_1_out, or_2_out, or_3_out, or_4_out, or_5_out, or_6_out, or_7_out,
       or_8_out, or_9_out, or_10_out, or_11_out, or_12_out, or_13_out, or_14_out, or_15_out, or_16_out,
       or_17_out, or_18_out, or_19_out, or_20_out, or_21_out, or_22_out, or_23_out, or_24_out, or_25_out,
       or_26_out, or_27_out, or_28_out, or_29_out, or_30_out, or_31_out, or_32_out;
  wire [7:0] and_8_out, and_16_out, and_24_out, and_33_out, two_complement_1_out_eight,
       two_complement_2_out_one, two_complement_3_out_one, two_complement_4_out_one, two_complement_5_out_one;

  and and_1 (and_8_out[7], custom_register_2_o_8, j_k_ff_1_qn);
  and and_2 (and_8_out[6], custom_register_2_o_7, j_k_ff_1_qn);
  and and_3 (and_8_out[5], custom_register_2_o_6, j_k_ff_1_qn);
  and and_4 (and_8_out[4], custom_register_2_o_5, j_k_ff_1_qn);
  and and_5 (and_8_out[3], custom_register_2_o_4, j_k_ff_1_qn);
  LED led_1 (.in(j_k_ff_1_q));
  and and_6 (and_8_out[2], custom_register_2_o_3, j_k_ff_1_qn);
  and and_7 (and_8_out[1], custom_register_2_o_2, j_k_ff_1_qn);
  or or_1 (or_1_out, and_8_out[7], two_complement_3_out_one[7]);
  LED led_2 (.in(or_1_out));
  and and_8 (and_8_out[0], custom_register_2_o_1, j_k_ff_1_qn);
  or or_2 (or_2_out, and_8_out[6], two_complement_3_out_one[6]);
  LED led_3 (.in(or_2_out));
  Button button_1 (.out(button_1_out));
  or or_3 (or_3_out, and_8_out[5], two_complement_3_out_one[5]);
  LED led_4 (.in(or_3_out));
  LED led_5 (.in(j_k_ff_1_q));
  J_K_Flip_Flop j_k_ff_1 (
    .J(1'b1), .K(1'b1), .clk(button_1_out), .Q(j_k_ff_1_q), .Qn(j_k_ff_1_qn));  // open: preset, reset
  or or_4 (or_4_out, and_8_out[4], two_complement_3_out_one[4]);
  LED led_6 (.in(or_4_out));
  Two_Complement two_complement_1 (
    .Eight(B_1), .Seven(B_2), .Six(B_3), .Five(B_4), .Four(B_5), .Three(B_6), .Two(B_7), .One(B_8),
    .Out_One(two_complement_1_out_eight[7]), .Out_Two(two_complement_1_out_eight[6]),
    .Out_Three(two_complement_1_out_eight[5]), .Out_Four(two_complement_1_out_eight[4]),
    .Out_Five(two_complement_1_out_eight[3]), .Out_Six(two_complement_1_out_eight[2]),
    .Out_Seven(two_complement_1_out_eight[1]), .Out_Eight(two_complement_1_out_eight[0]));  // open: Toggle, Pos_or_Neg
  Custom_Register custom_register_1 ();  // open: i_1, i_2, i_3, i_4, i_5, i_6, i_7, i_8, Clock, Reset, O_1, O_2, O_3, O_4, O_5, O_6, O_7, O_8
  or or_5 (or_5_out, and_8_out[3], two_complement_3_out_one[3]);
  LED led_7 (.in(or_5_out));
  or or_6 (or_6_out, two_complement_4_out_one[7], and_24_out[7]);
  Calculating_adder calculating_adder_1 ();  // open: Reset, Add, A_1, B_1, A_2, B_2, A_3, B_3, A_4, B_4, A_5, B_5, A_6, B_6, A_7, B_7, A_8, B_8, O_1, O_2, O_3, O_4, O_5, O_6, O_7, O_8, Overflow
  or or_7 (or_7_out, and_8_out[2], two_complement_3_out_one[2]);
  LED led_8 (.in(or_7_out));
  or or_8 (or_8_out, two_complement_4_out_one[6], and_24_out[6]);
  Button button_2 (.out(button_2_out));
  Button button_3 (.out(button_3_out));
  and and_9 (and_16_out[7], j_k_ff_1_q, custom_register_2_o_8);
  and and_10 (and_16_out[6], j_k_ff_1_q, custom_register_2_o_7);
  or or_9 (or_9_out, and_8_out[1], two_complement_3_out_one[1]);
  LED led_9 (.in(or_9_out));
  or or_10 (or_10_out, two_complement_4_out_one[5], and_24_out[5]);
  and and_11 (and_16_out[5], j_k_ff_1_q, custom_register_2_o_6);
  and and_12 (and_16_out[4], j_k_ff_1_q, custom_register_2_o_5);
  or or_11 (or_11_out, and_8_out[0], two_complement_3_out_one[0]);
  LED led_10 (.in(or_11_out));
  or or_12 (or_12_out, two_complement_4_out_one[4], and_24_out[4]);
  or or_13 (or_13_out, two_complement_4_out_one[3], and_24_out[3]);
  and and_13 (and_16_out[3], j_k_ff_1_q, custom_register_2_o_4);
  and and_14 (and_16_out[2], j_k_ff_1_q, custom_register_2_o_3);
  or or_14 (or_14_out, two_complement_4_out_one[2], and_24_out[2]);
  Custom_Register custom_register_2 (
    .i_1(in_8), .i_2(in_7), .i_3(in_6), .i_4(in_5), .i_5(Input_A), .i_6(in_3), .i_7(in_2), .i_8(in_1),
    .Clock(button_2_out), .Reset(button_3_out), .O_1(custom_register_2_o_1), .O_2(custom_register_2_o_2),
    .O_3(custom_register_2_o_3), .O_4(custom_register_2_o_4), .O_5(custom_register_2_o_5),
    .O_6(custom_register_2_o_6), .O_7(custom_register_2_o_7), .O_8(custom_register_2_o_8));
  and and_15 (and_16_out[1], j_k_ff_1_q, custom_register_2_o_2);
  and and_16 (and_16_out[0], j_k_ff_1_q, custom_register_2_o_1);
  Two_Complement two_complement_2 (
    .Eight(and_16_out[7]), .Seven(and_16_out[6]), .Six(and_16_out[5]), .Five(and_16_out[4]),
    .Four(and_16_out[3]), .Three(and_16_out[2]), .Two(and_16_out[1]), .One(and_16_out[0]), .Toggle(1'b1),
    .Out_One(two_complement_2_out_one[0]), .Out_Two(two_complement_2_out_one[1]),
    .Out_Three(two_complement_2_out_one[2]), .Out_Four(two_complement_2_out_one[3]),
    .Out_Five(two_complement_2_out_one[4]), .Out_Six(two_complement_2_out_one[5]),
    .Out_Seven(two_complement_2_out_one[6]), .Out_Eight(two_complement_2_out_one[7]));  // open: Pos_or_Neg
  Two_Complement two_complement_3 (
    .Eight(two_complement_2_out_one[7]), .Seven(two_complement_2_out_one[6]),
    .Six(two_complement_2_out_one[5]), .Five(two_complement_2_out_one[4]),
    .Four(two_complement_2_out_one[3]), .Three(two_complement_2_out_one[2]),
    .Two(two_complement_2_out_one[1]), .One(two_complement_2_out_one[0]), .Toggle(1'b1),
    .Out_One(two_complement_3_out_one[0]), .Out_Two(two_complement_3_out_one[1]),
    .Out_Three(two_complement_3_out_one[2]), .Out_Four(two_complement_3_out_one[3]),
    .Out_Five(two_complement_3_out_one[4]), .Out_Six(two_complement_3_out_one[5]),
    .Out_Seven(two_complement_3_out_one[6]), .Out_Eight(two_complement_3_out_one[7]));  // open: Pos_or_Neg
  or or_15 (or_15_out, two_complement_4_out_one[1], and_24_out[1]);
  or or_16 (or_16_out, two_complement_4_out_one[0], and_24_out[0]);
  or or_17 (or_17_out, and_8_out[7], two_complement_2_out_one[7]);
  and and_17 (and_24_out[7], custom_register_3_o_8, j_k_ff_2_qn);
  or or_18 (or_18_out, and_8_out[6], two_complement_2_out_one[6]);
  and and_18 (and_24_out[6], custom_register_3_o_7, j_k_ff_2_qn);
  and and_19 (and_24_out[5], custom_register_3_o_6, j_k_ff_2_qn);
  or or_19 (or_19_out, and_8_out[5], two_complement_2_out_one[5]);
  and and_20 (and_24_out[4], custom_register_3_o_5, j_k_ff_2_qn);
  and and_21 (and_24_out[3], custom_register_3_o_4, j_k_ff_2_qn);
  LED led_11 (.in(j_k_ff_2_q));
  or or_20 (or_20_out, and_8_out[4], two_complement_2_out_one[4]);
  and and_22 (and_24_out[2], custom_register_3_o_3, j_k_ff_2_qn);
  and and_23 (and_24_out[1], custom_register_3_o_2, j_k_ff_2_qn);
  or or_21 (or_21_out, and_8_out[3], two_complement_2_out_one[3]);
  and and_24 (and_24_out[0], custom_register_3_o_1, j_k_ff_2_qn);
  or or_22 (or_22_out, and_24_out[7], two_complement_5_out_one[7]);
  or or_23 (or_23_out, and_24_out[6], two_complement_5_out_one[6]);
  LED led_12 (.in(or_22_out));
  LED led_13 (.in(or_23_out));
  or or_24 (or_24_out, and_8_out[2], two_complement_2_out_one[2]);
  Button button_4 (.out(button_4_out));
  or or_25 (or_25_out, and_24_out[5], two_complement_5_out_one[5]);
  LED led_14 (.in(or_25_out));
  and and_25 (and_25_out, in_9, j_k_ff_3_q);
  or or_26 (or_26_out, and_8_out[1], two_complement_2_out_one[1]);
  or or_27 (or_27_out, and_8_out[0], two_complement_2_out_one[0]);
  J_K_Flip_Flop j_k_ff_2 (
    .J(1'b1), .K(1'b1), .clk(button_4_out), .Q(j_k_ff_2_q), .Qn(j_k_ff_2_qn));  // open: preset, reset
  or or_28 (or_28_out, and_24_out[4], two_complement_5_out_one[4]);
  LED led_15 (.in(or_28_out));
  LED led_16 (.in(j_k_ff_2_q));
  or or_29 (or_29_out, and_24_out[3], two_complement_5_out_one[3]);
  LED led_17 (.in(or_29_out));
  Button button_5 (.out(button_5_out));
  Button button_6 (.out(button_6_out));
  Clock clock_1 (.out(clock_1_out));
  or or_30 (or_30_out, and_24_out[2], two_complement_5_out_one[2]);
  LED led_18 (.in(or_30_out));
  Button button_7 (.out(button_7_out));
  Button button_8 (.out(button_8_out));
  and and_26 (and_33_out[7], j_k_ff_2_q, custom_register_3_o_8);
  and and_27 (and_33_out[6], j_k_ff_2_q, custom_register_3_o_7);
  or or_31 (or_31_out, and_24_out[1], two_complement_5_out_one[1]);
  LED led_19 (.in(or_31_out));
  J_K_Flip_Flop j_k_ff_3 (
    .J(button_5_out), .K(button_6_out), .clk(clock_1_out), .Q(j_k_ff_3_q), .Qn(j_k_ff_3_qn));  // open: preset, reset
  and and_28 (and_33_out[5], j_k_ff_2_q, custom_register_3_o_6);
  and and_29 (and_33_out[4], j_k_ff_2_q, custom_register_3_o_5);
  or or_32 (or_32_out, and_24_out[0], two_complement_5_out_one[0]);
  LED led_20 (.in(or_32_out));
  and and_30 (and_33_out[3], j_k_ff_2_q, custom_register_3_o_4);
  and and_31 (and_33_out[2], j_k_ff_2_q, custom_register_3_o_3);
  Custom_Register custom_register_3 (
    .i_1(in_17), .i_2(in_16), .i_3(in_15), .i_4(in_14), .i_5(Input_B), .i_6(in_12), .i_7(in_11), .i_8(in_10),
    .Clock(button_7_out), .Reset(button_8_out), .O_1(custom_register_3_o_1), .O_2(custom_register_3_o_2),
    .O_3(custom_register_3_o_3), .O_4(custom_register_3_o_4), .O_5(custom_register_3_o_5),
    .O_6(custom_register_3_o_6), .O_7(custom_register_3_o_7), .O_8(custom_register_3_o_8));
  and and_32 (and_33_out[1], j_k_ff_2_q, custom_register_3_o_2);
  and and_33 (and_33_out[0], j_k_ff_2_q, custom_register_3_o_1);
  Two_Complement two_complement_4 (
    .Eight(and_33_out[7]), .Seven(and_33_out[6]), .Six(and_33_out[5]), .Five(and_33_out[4]),
    .Four(and_33_out[3]), .Three(and_33_out[2]), .Two(and_33_out[1]), .One(and_33_out[0]), .Toggle(1'b1),
    .Out_One(two_complement_4_out_one[0]), .Out_Two(two_complement_4_out_one[1]),
    .Out_Three(two_complement_4_out_one[2]), .Out_Four(two_complement_4_out_one[3]),
    .Out_Five(two_complement_4_out_one[4]), .Out_Six(two_complement_4_out_one[5]),
    .Out_Seven(two_complement_4_out_one[6]), .Out_Eight(two_complement_4_out_one[7]));  // open: Pos_or_Neg
  Two_Complement two_complement_5 (
    .Eight(two_complement_4_out_one[7]), .Seven(two_complement_4_out_one[6]),
    .Six(two_complement_4_out_one[5]), .Five(two_complement_4_out_one[4]),
    .Four(two_complement_4_out_one[3]), .Three(two_complement_4_out_one[2]),
    .Two(two_complement_4_out_one[1]), .One(two_complement_4_out_one[0]), .Toggle(1'b1),
    .Out_One(two_complement_5_out_one[0]), .Out_Two(two_complement_5_out_one[1]),
    .Out_Three(two_complement_5_out_one[2]), .Out_Four(two_complement_5_out_one[3]),
    .Out_Five(two_complement_5_out_one[4]), .Out_Six(two_complement_5_out_one[5]),
    .Out_Seven(two_complement_5_out_one[6]), .Out_Eight(two_complement_5_out_one[7]));  // open: Pos_or_Neg
  and and_34 (and_34_out, j_k_ff_3_qn, in_9);

  // Notes on the sheet:
  //   +/-
  //   +/-
  //   Load
  //   Reset
  //   +/-
  //   +/-
  //   Load
  //   Reset
endmodule

module Two_Complement (
  input  Eight,
  input  Seven,
  input  Six,
  input  Five,
  input  Four,
  input  Three,
  input  Two,
  input  One,
  input  Toggle,
  output Pos_or_Neg,
  output Out_One,
  output Out_Two,
  output Out_Three,
  output Out_Four,
  output Out_Five,
  output Out_Six,
  output Out_Seven,
  output Out_Eight
);

  wire [7:0] xor_8_out;

  J_K_Flip_Flop j_k_ff_1 (.J(1'b1), .K(1'b1), .clk(Toggle), .Q(Pos_or_Neg));  // open: Qn, preset, reset
  xor xor_1 (xor_8_out[7], Pos_or_Neg, Eight);
  xor xor_2 (xor_8_out[6], Pos_or_Neg, Seven);
  xor xor_3 (xor_8_out[5], Pos_or_Neg, Six);
  xor xor_4 (xor_8_out[4], Pos_or_Neg, Five);
  xor xor_5 (xor_8_out[3], Pos_or_Neg, Four);
  xor xor_6 (xor_8_out[2], Pos_or_Neg, Three);
  xor xor_7 (xor_8_out[1], Pos_or_Neg, Two);
  Eight_bit_adder eight_bit_adder_1 (
    .A_1(xor_8_out[0]), .B_1(Pos_or_Neg), .A_2(xor_8_out[1]), .A_3(xor_8_out[2]), .A_4(xor_8_out[3]),
    .A_5(xor_8_out[4]), .A_6(xor_8_out[5]), .A_7(xor_8_out[6]), .A_8(xor_8_out[7]), .O_1(Out_One),
    .O_2(Out_Two), .O_3(Out_Three), .O_4(Out_Four), .O_5(Out_Five), .O_6(Out_Six), .O_7(Out_Seven),
    .O_8(Out_Eight));  // open: B_2, B_3, B_4, B_5, B_6, B_7, B_8, Overflow
  xor xor_8 (xor_8_out[0], Pos_or_Neg, One);
endmodule

module Sub_tractor (
  input  Subtract,
  input  Reset,
  input  A_1,
  input  A_2,
  input  A_3,
  input  A_4,
  input  A_5,
  input  A_6,
  input  A_7,
  input  A_8,
  input  B_1,
  input  B_2,
  input  B_3,
  input  B_4,
  input  B_5,
  input  B_6,
  input  B_7,
  input  B_8,
  output O_1,
  output O_2,
  output O_3,
  output O_4,
  output O_5,
  output O_6,
  output O_7,
  output O_8
);

  wire [7:0] two_complement_1_out_one;

  Two_Complement two_complement_1 (
    .Eight(B_8), .Seven(B_7), .Six(B_6), .Five(B_5), .Four(B_4), .Three(B_3), .Two(B_2), .One(B_1),
    .Toggle(1'b1), .Out_One(two_complement_1_out_one[0]), .Out_Two(two_complement_1_out_one[1]),
    .Out_Three(two_complement_1_out_one[2]), .Out_Four(two_complement_1_out_one[3]),
    .Out_Five(two_complement_1_out_one[4]), .Out_Six(two_complement_1_out_one[5]),
    .Out_Seven(two_complement_1_out_one[6]), .Out_Eight(two_complement_1_out_one[7]));  // open: Pos_or_Neg
  Calculating_adder calculating_adder_1 (
    .Reset(Reset), .Add(Subtract), .A_1(A_1), .B_1(two_complement_1_out_one[0]), .A_2(A_2),
    .B_2(two_complement_1_out_one[1]), .A_3(A_3), .B_3(two_complement_1_out_one[2]), .A_4(A_4),
    .B_4(two_complement_1_out_one[3]), .A_5(A_5), .B_5(two_complement_1_out_one[4]), .A_6(A_6),
    .B_6(two_complement_1_out_one[5]), .A_7(A_7), .B_7(two_complement_1_out_one[6]), .A_8(A_8),
    .B_8(two_complement_1_out_one[7]), .O_1(O_1), .O_2(O_2), .O_3(O_3), .O_4(O_4), .O_5(O_5), .O_6(O_6),
    .O_7(O_7), .O_8(O_8));  // open: Overflow
endmodule

module Calculator_Adder_and_Subtractor (
  input  A_8,
  input  A_7,
  input  A_6,
  input  A_5,
  input  A_4,
  input  A_3,
  input  A_2,
  input  A_1,
  input  B_8,
  input  B_7,
  input  B_6,
  input  B_5,
  input  B_4,
  input  B_3,
  input  B_2,
  input  B_1,
  input  Reset,
  input  Add,
  input  Subtract,
  output O_8,
  output O_7,
  output O_6,
  output O_5,
  output O_4,
  output O_3,
  output O_2,
  output O_1
);

  wire clock_1_out, j_k_ff_1_q, j_k_ff_1_qn;
  wire [7:0] and_8_out, and_16_out, and_24_out, and_32_out, calculating_adder_1_o_1, sub_tractor_1_o_1;

  and and_1 (and_8_out[7], j_k_ff_1_qn, B_8);
  and and_2 (and_8_out[6], j_k_ff_1_qn, B_7);
  and and_3 (and_8_out[5], j_k_ff_1_qn, B_6);
  and and_4 (and_8_out[4], j_k_ff_1_qn, B_5);
  and and_5 (and_8_out[3], j_k_ff_1_qn, B_4);
  and and_6 (and_8_out[2], j_k_ff_1_qn, B_3);
  and and_7 (and_8_out[1], j_k_ff_1_qn, B_2);
  and and_8 (and_8_out[0], j_k_ff_1_qn, B_1);
  and and_9 (and_16_out[7], j_k_ff_1_qn, A_8);
  and and_10 (and_16_out[6], j_k_ff_1_qn, A_7);
  and and_11 (and_16_out[5], j_k_ff_1_qn, A_6);
  and and_12 (and_16_out[4], j_k_ff_1_qn, A_5);
  and and_13 (and_16_out[2], j_k_ff_1_qn, A_3);
  and and_14 (and_16_out[3], j_k_ff_1_qn, A_4);
  and and_15 (and_16_out[1], j_k_ff_1_qn, A_2);
  and and_16 (and_16_out[0], j_k_ff_1_qn, A_1);
  Calculating_adder calculating_adder_1 (
    .Reset(Reset), .Add(Add), .A_1(and_16_out[0]), .B_1(and_8_out[0]), .A_2(and_16_out[1]),
    .B_2(and_8_out[1]), .A_3(and_16_out[2]), .B_3(and_8_out[2]), .A_4(and_16_out[3]), .B_4(and_8_out[3]),
    .A_5(and_16_out[4]), .B_5(and_8_out[4]), .A_6(and_16_out[5]), .B_6(and_8_out[5]), .A_7(and_16_out[6]),
    .B_7(and_8_out[6]), .A_8(and_16_out[7]), .B_8(and_8_out[7]), .O_1(calculating_adder_1_o_1[0]),
    .O_2(calculating_adder_1_o_1[1]), .O_3(calculating_adder_1_o_1[2]), .O_4(calculating_adder_1_o_1[3]),
    .O_5(calculating_adder_1_o_1[4]), .O_6(calculating_adder_1_o_1[5]), .O_7(calculating_adder_1_o_1[6]),
    .O_8(calculating_adder_1_o_1[7]));  // open: Overflow
  or or_1 (O_8, sub_tractor_1_o_1[7], calculating_adder_1_o_1[7]);
  and and_17 (and_24_out[7], j_k_ff_1_q, B_8);
  or or_2 (O_7, sub_tractor_1_o_1[6], calculating_adder_1_o_1[6]);
  and and_18 (and_24_out[6], j_k_ff_1_q, B_7);
  and and_19 (and_24_out[5], j_k_ff_1_q, B_6);
  or or_3 (O_6, sub_tractor_1_o_1[5], calculating_adder_1_o_1[5]);
  or or_4 (O_5, sub_tractor_1_o_1[4], calculating_adder_1_o_1[4]);
  and and_20 (and_24_out[4], j_k_ff_1_q, B_5);
  and and_21 (and_24_out[3], j_k_ff_1_q, B_4);
  or or_5 (O_4, sub_tractor_1_o_1[3], calculating_adder_1_o_1[3]);
  and and_22 (and_24_out[2], j_k_ff_1_q, B_3);
  and and_23 (and_24_out[1], j_k_ff_1_q, B_2);
  or or_6 (O_3, sub_tractor_1_o_1[2], calculating_adder_1_o_1[2]);
  and and_24 (and_24_out[0], j_k_ff_1_q, B_1);
  or or_7 (O_2, sub_tractor_1_o_1[1], calculating_adder_1_o_1[1]);
  or or_8 (O_1, sub_tractor_1_o_1[0], calculating_adder_1_o_1[0]);
  and and_25 (and_32_out[7], j_k_ff_1_q, A_8);
  and and_26 (and_32_out[6], j_k_ff_1_q, A_7);
  and and_27 (and_32_out[5], j_k_ff_1_q, A_6);
  and and_28 (and_32_out[4], j_k_ff_1_q, A_5);
  and and_29 (and_32_out[3], j_k_ff_1_q, A_4);
  Sub_tractor sub_tractor_1 (
    .Subtract(Subtract), .Reset(Reset), .A_1(and_32_out[0]), .A_2(and_32_out[1]), .A_3(and_32_out[2]),
    .A_4(and_32_out[3]), .A_5(and_32_out[4]), .A_6(and_32_out[5]), .A_7(and_32_out[6]), .A_8(and_32_out[7]),
    .B_1(and_24_out[0]), .B_2(and_24_out[1]), .B_3(and_24_out[2]), .B_4(and_24_out[3]), .B_5(and_24_out[4]),
    .B_6(and_24_out[5]), .B_7(and_24_out[6]), .B_8(and_24_out[7]), .O_1(sub_tractor_1_o_1[0]),
    .O_2(sub_tractor_1_o_1[1]), .O_3(sub_tractor_1_o_1[2]), .O_4(sub_tractor_1_o_1[3]),
    .O_5(sub_tractor_1_o_1[4]), .O_6(sub_tractor_1_o_1[5]), .O_7(sub_tractor_1_o_1[6]),
    .O_8(sub_tractor_1_o_1[7]));
  and and_30 (and_32_out[2], j_k_ff_1_q, A_3);
  and and_31 (and_32_out[1], j_k_ff_1_q, A_2);
  and and_32 (and_32_out[0], j_k_ff_1_q, A_1);
  J_K_Flip_Flop j_k_ff_1 (
    .J(Subtract), .K(Add), .clk(clock_1_out), .Q(j_k_ff_1_q), .Qn(j_k_ff_1_qn));  // open: preset, reset
  Clock clock_1 (.out(clock_1_out));
endmodule

module Pos_Neg_Output (
  input  i_8,
  input  i_7,
  input  i_6,
  input  i_5,
  input  i_4,
  input  i_3,
  input  i_2,
  input  i_1,
  output O_8,
  output O_7,
  output O_6,
  output O_5,
  output O_4,
  output O_3,
  output O_2,
  output O_1,
  output Pos_or_Neg
);

  wire not_1_out, not_2_out;
  wire [7:0] and_8_out, and_16_out, two_complement_1_out_eight;

  not not_1 (not_1_out, i_8);
  and and_1 (and_8_out[7], not_1_out, i_8);
  and and_2 (and_8_out[6], not_1_out, i_7);
  and and_3 (and_8_out[5], not_1_out, i_6);
  and and_4 (and_8_out[4], not_1_out, i_5);
  and and_5 (and_8_out[3], not_1_out, i_4);
  and and_6 (and_8_out[2], not_1_out, i_3);
  and and_7 (and_8_out[1], not_1_out, i_2);
  or or_1 (O_8, two_complement_1_out_eight[7], and_8_out[7]);
  and and_8 (and_8_out[0], not_1_out, i_1);
  or or_2 (O_7, two_complement_1_out_eight[6], and_8_out[6]);
  or or_3 (O_6, two_complement_1_out_eight[5], and_8_out[5]);
  or or_4 (O_5, two_complement_1_out_eight[4], and_8_out[4]);
  not not_2 (not_2_out, not_1_out);
  or or_5 (O_4, two_complement_1_out_eight[3], and_8_out[3]);
  and and_9 (and_16_out[7], i_8, not_2_out);
  or or_6 (O_3, two_complement_1_out_eight[2], and_8_out[2]);
  and and_10 (and_16_out[6], i_7, not_2_out);
  or or_7 (O_2, two_complement_1_out_eight[1], and_8_out[1]);
  or or_8 (O_1, two_complement_1_out_eight[0], and_8_out[0]);
  and and_11 (and_16_out[5], i_6, not_2_out);
  and and_12 (and_16_out[4], i_5, not_2_out);
  and and_13 (and_16_out[3], i_4, not_2_out);
  and and_14 (and_16_out[2], i_3, not_2_out);
  and and_15 (and_16_out[1], i_2, not_2_out);
  and and_16 (and_16_out[0], i_1, not_2_out);
  Two_Complement two_complement_1 (
    .Eight(and_16_out[7]), .Seven(and_16_out[6]), .Six(and_16_out[5]), .Five(and_16_out[4]),
    .Four(and_16_out[3]), .Three(and_16_out[2]), .Two(and_16_out[1]), .One(and_16_out[0]), .Toggle(1'b1),
    .Out_One(two_complement_1_out_eight[7]), .Out_Two(two_complement_1_out_eight[6]),
    .Out_Three(two_complement_1_out_eight[5]), .Out_Four(two_complement_1_out_eight[4]),
    .Out_Five(two_complement_1_out_eight[3]), .Out_Six(two_complement_1_out_eight[2]),
    .Out_Seven(two_complement_1_out_eight[1]), .Out_Eight(two_complement_1_out_eight[0]));  // open: Pos_or_Neg

  assign Pos_or_Neg = i_8;
endmodule
