// Logisim project stage1.circ as structural Verilog: 2 circuits, main circuit interface
module \interface  (
  input  in_1,
  input  in_2,
  input  in_3,
  input  Input_B_Display,
  input  in_5,
  input  in_6,
  input  in_7,
  input  in_8,
  input  in_9,
  input  in_10,
  input  in_11,
  input  Input_A,
  input  in_13,
  input  in_14,
  input  in_15,
  input  in_16,
  input  in_17,
  input  in_18,
  input  in_19,
  input  in_20,
  input  in_21,
  input  in_22,
  input  in_23,
  input  in_24
);

  wire button_2_out, button_3_out, button_9_out, button_10_out;
  wire [7:0] custom_register_1_o_1, custom_register_2_o_1;

  Button button_1 ();  // open: out
  LED led_1 ();  // open: in
  Button button_2 (.out(button_2_out));
  Button button_3 (.out(button_3_out));
  LED led_2 (.in(custom_register_1_o_1[7]));
  LED led_3 (.in(custom_register_1_o_1[6]));
  LED led_4 ();  // open: in
  Button button_4 ();  // open: out
  Button button_5 ();  // open: out
  Button button_6 ();  // open: out
  Button button_7 ();  // open: out
  LED led_5 (.in(custom_register_1_o_1[5]));
  LED led_6 (.in(custom_register_1_o_1[4]));
  LED led_7 ();  // open: in
  LED led_8 (.in(custom_register_1_o_1[3]));
  LED led_9 (.in(custom_register_1_o_1[2]));
  LED led_10 ();  // open: in
  LED led_11 ();  // open: in
  LED led_12 (.in(custom_register_1_o_1[1]));
  LED led_13 (.in(custom_register_1_o_1[0]));
  LED led_14 ();  // open: in
  LED led_15 ();  // open: in
  Custom_Register custom_register_1 (
    .i_1(in_16), .i_2(in_15), .i_3(in_14), .i_4(in_13), .i_5(Input_A), .i_6(in_11), .i_7(in_10), .i_8(in_9),
    .Clock(button_2_out), .Reset(button_3_out), .O_1(custom_register_1_o_1[0]),
    .O_2(custom_register_1_o_1[1]), .O_3(custom_register_1_o_1[2]), .O_4(custom_register_1_o_1[3]),
    .O_5(custom_register_1_o_1[4]), .O_6(custom_register_1_o_1[5]), .O_7(custom_register_1_o_1[6]),
    .O_8(custom_register_1_o_1[7]));
  LED led_16 ();  // open: in
  LED led_17 ();  // open: in
  LED led_18 ();  // open: in
  LED led_19 ();  // open: in
  LED led_20 ();  // open: in
  Button button_8 ();  // open: out
  LED led_21 ();  // open: in
  LED led_22 ();  // open: in
  LED led_23 ();  // open: in
  LED led_24 ();  // open: in
  LED led_25 ();  // open: in
  LED led_26 (.in(custom_register_2_o_1[7]));
  LED led_27 ();  // open: in
  LED led_28 ();  // open: in
  LED led_29 ();  // open: in
  Button button_9 (.out(button_9_out));
  Button button_10 (.out(button_10_out));
  LED led_30 (.in(custom_register_2_o_1[6]));
  LED led_31 (.in(custom_register_2_o_1[5]));
  LED led_32 ();  // open: in
  LED led_33 ();  // open: in
  LED led_34 ();  // open: in
  LED led_35 (.in(custom_register_2_o_1[4]));
  LED led_36 (.in(custom_register_2_o_1[3]));
  LED led_37 ();  // open: in
  LED led_38 ();  // open: in
  LED led_39 (.in(custom_register_2_o_1[1]));
  LED led_40 (.in(custom_register_2_o_1[2]));
  LED led_41 ();  // open: in
  Custom_Register custom_register_2 (
    .i_1(in_24), .i_2(in_23), .i_3(in_22), .i_4(in_21), .i_5(in_20), .i_6(in_19), .i_7(in_18), .i_8(in_17),
    .Clock(button_9_out), .Reset(button_10_out), .O_1(custom_register_2_o_1[0]),
    .O_2(custom_register_2_o_1[1]), .O_3(custom_register_2_o_1[2]), .O_4(custom_register_2_o_1[3]),
    .O_5(custom_register_2_o_1[4]), .O_6(custom_register_2_o_1[5]), .O_7(custom_register_2_o_1[6]),
    .O_8(custom_register_2_o_1[7]));
  LED led_42 (.in(custom_register_2_o_1[0]));
  LED led_43 ();  // open: in

  // Notes on the sheet:
  //   +/-
  //   +/-
  //   Load
  //   Add
  //   Subtract
  //   Reset
  //   Load
  //   Reset
  //   Input A Display
  //   +/-
  //   8 bit Binary Calculator
  //   +/-
  //   +/-
  //   Output
  //   Load
  //   Reset
  //   Input B
  //   Input B
endmodule

module Custom_Register (
  input  i_1,
  input  i_2,
  input  i_3,
  input  i_4,
  input  i_5,
  input  i_6,
  input  i_7,
  input  i_8,
  input  Clock,
  input  Reset,
  output O_1,
  output O_2,
  output O_3,
  output O_4,
  output O_5,
  output O_6,
  output O_7,
  output O_8
);

  D_Flip_Flop d_ff_1 (.D(i_1), .clk(Clock), .Q(O_1), .reset(Reset));  // open: Qn, preset
  D_Flip_Flop d_ff_2 (.D(i_2), .clk(Clock), .Q(O_2), .reset(Reset));  // open: Qn, preset
  D_Flip_Flop d_ff_3 (.D(i_3), .clk(Clock), .Q(O_3), .reset(Reset));  // open: Qn, preset
  D_Flip_Flop d_ff_4 (.D(i_4), .clk(Clock), .Q(O_4), .reset(Reset));  // open: Qn, preset
  D_Flip_Flop d_ff_5 (.D(i_5), .clk(Clock), .Q(O_5), .reset(Reset));  // open: Qn, preset
  D_Flip_Flop d_ff_6 (.D(i_6), .clk(Clock), .Q(O_6), .reset(Reset));  // open: Qn, preset
  D_Flip_Flop d_ff_7 (.D(i_7), .clk(Clock), .Q(O_7), .reset(Reset));  // open: Qn, preset
  D_Flip_Flop d_ff_8 (.D(i_8), .clk(Clock), .Q(O_8), .reset(Reset));  // open: Qn, preset
endmodule
