// Logisim project stage2.circ as structural Verilog: 7 circuits, main circuit interface
module \interface  (
  input  in_1,
  input  in_2,
  input  in_3,
  input  Input_B_Display,
  input  in_5,
  input  in_6,
  input  in_7,
  input  in_8,
  input  in_9,
  input  in_10,
  input  in_11,
  input  Input_A,
  input  in_13,
  input  in_14,
  input  in_15,
  input  in_16,
  input  in_17,
  input  in_18,
  input  in_19,
  input  Input_B,
  input  in_21,
  input  in_22,
  input  in_23,
  input  in_24
);

  wire button_2_out, button_3_out, button_8_out, button_9_out, button_10_out, button_11_out,
       calculating_adder_1_out_19, calculating_adder_1_out_20, calculating_adder_1_out_21,
       calculating_adder_1_out_22, calculating_adder_1_out_23, calculating_adder_1_out_24,
       calculating_adder_1_out_25, calculating_adder_1_out_26, calculating_adder_1_overflow;
  wire [7:0] custom_register_1_o_1, custom_register_2_o_1;

  Button button_1 ();  // open: out
  LED led_1 ();  // open: in
  Button button_2 (.out(button_2_out));
  Button button_3 (.out(button_3_out));
  LED led_2 (.in(custom_register_1_o_1[7]));
  LED led_3 (.in(custom_register_1_o_1[6]));
  LED led_4 ();  // open: in
  Button button_4 ();  // open: out
  Button button_5 ();  // open: out
  Button button_6 ();  // open: out
  LED led_5 (.in(custom_register_1_o_1[5]));
  LED led_6 (.in(custom_register_1_o_1[4]));
  LED led_7 ();  // open: in
  LED led_8 (.in(custom_register_1_o_1[3]));
  LED led_9 (.in(custom_register_1_o_1[2]));
  LED led_10 ();  // open: in
  LED led_11 ();  // open: in
  LED led_12 (.in(custom_register_1_o_1[1]));
  LED led_13 (.in(custom_register_1_o_1[0]));
  LED led_14 ();  // open: in
  LED led_15 ();  // open: in
  Custom_Register custom_register_1 (
    .i_1(in_16), .i_2(in_15), .i_3(in_14), .i_4(in_13), .i_5(Input_A), .i_6(in_11), .i_7(in_10), .i_8(in_9),
    .Clock(button_2_out), .Reset(button_3_out), .O_1(custom_register_1_o_1[0]),
    .O_2(custom_register_1_o_1[1]), .O_3(custom_register_1_o_1[2]), .O_4(custom_register_1_o_1[3]),
    .O_5(custom_register_1_o_1[4]), .O_6(custom_register_1_o_1[5]), .O_7(custom_register_1_o_1[6]),
    .O_8(custom_register_1_o_1[7]));
  LED led_16 ();  // open: in
  LED led_17 ();  // open: in
  LED led_18 ();  // open: in
  LED led_19 ();  // open: in
  LED led_20 ();  // open: in
  LED led_21 (.in(calculating_adder_1_overflow));
  LED led_22 (.in(calculating_adder_1_out_26));
  Button button_7 ();  // open: out
  LED led_23 ();  // open: in
  LED led_24 ();  // open: in
  LED led_25 ();  // open: in
  LED led_26 (.in(custom_register_2_o_1[7]));
  LED led_27 (.in(calculating_adder_1_out_25));
  LED led_28 (.in(calculating_adder_1_out_24));
  LED led_29 (.in(calculating_adder_1_out_23));
  LED led_30 (.in(calculating_adder_1_out_22));
  LED led_31 ();  // open: in
  LED led_32 ();  // open: in
  Button button_8 (.out(button_8_out));
  Button button_9 (.out(button_9_out));
  LED led_33 (.in(custom_register_2_o_1[6]));
  LED led_34 (.in(custom_register_2_o_1[5]));
  Calculating_adder calculating_adder_1 (
    .Reset(button_11_out), .Add(button_10_out), .A_1(custom_register_1_o_1[0]),
    .B_1(custom_register_2_o_1[0]), .A_2(custom_register_1_o_1[1]), .B_2(custom_register_2_o_1[1]),
    .A_3(custom_register_1_o_1[2]), .B_3(custom_register_2_o_1[2]), .A_4(custom_register_1_o_1[3]),
    .B_4(custom_register_2_o_1[3]), .A_5(custom_register_1_o_1[4]), .B_5(custom_register_2_o_1[4]),
    .A_6(custom_register_1_o_1[5]), .B_6(custom_register_2_o_1[5]), .A_7(custom_register_1_o_1[6]),
    .B_7(custom_register_2_o_1[6]), .A_8(custom_register_1_o_1[7]), .B_8(custom_register_2_o_1[7]),
    .out_19(calculating_adder_1_out_19), .out_20(calculating_adder_1_out_20),
    .out_21(calculating_adder_1_out_21), .out_22(calculating_adder_1_out_22),
    .out_23(calculating_adder_1_out_23), .out_24(calculating_adder_1_out_24),
    .out_25(calculating_adder_1_out_25), .out_26(calculating_adder_1_out_26),
    .Overflow(calculating_adder_1_overflow));
  LED led_35 (.in(calculating_adder_1_out_21));
  LED led_36 (.in(calculating_adder_1_out_20));
  LED led_37 (.in(calculating_adder_1_out_19));
  LED led_38 ();  // open: in
  LED led_39 ();  // open: in
  LED led_40 ();  // open: in
  LED led_41 (.in(custom_register_2_o_1[4]));
  LED led_42 (.in(custom_register_2_o_1[3]));
  LED led_43 ();  // open: in
  LED led_44 ();  // open: in
  LED led_45 ();  // open: in
  LED led_46 (.in(custom_register_2_o_1[2]));
  LED led_47 (.in(custom_register_2_o_1[1]));
  Button button_10 (.out(button_10_out));
  Button button_11 (.out(button_11_out));
  LED led_48 ();  // open: in
  LED led_49 ();  // open: in
  Custom_Register custom_register_2 (
    .i_1(in_24), .i_2(in_23), .i_3(in_22), .i_4(in_21), .i_5(Input_B), .i_6(in_19), .i_7(in_18), .i_8(in_17),
    .Clock(button_8_out), .Reset(button_9_out), .O_1(custom_register_2_o_1[0]),
    .O_2(custom_register_2_o_1[1]), .O_3(custom_register_2_o_1[2]), .O_4(custom_register_2_o_1[3]),
    .O_5(custom_register_2_o_1[4]), .O_6(custom_register_2_o_1[5]), .O_7(custom_register_2_o_1[6]),
    .O_8(custom_register_2_o_1[7]));
  LED led_50 (.in(custom_register_2_o_1[0]));
  LED led_51 ();  // open: in
  LED led_52 ();  // open: in

  // Notes on the sheet:
  //   +/-
  //   +/-
  //   Load
  //   Subtract
  //   Reset
  //   Load
  //   Reset
  //   Input A Display
  //   +/-
  //   8 bit Binary Calculator
  //   +/-
  //   +/-
  //   Output
  //   Load
  //   Reset
  //   Input B
  //   Add
  //   Reset
endmodule

module Custom_Register (
  input  i_1,
  input  i_2,
  input  i_3,
  input  i_4,
  input  i_5,
  input  i_6,
  input  i_7,
  input  i_8,
  input  Clock,
  input  Reset,
  output O_1,
  output O_2,
  output O_3,
  output O_4,
  output O_5,
  output O_6,
  output O_7,
  output O_8
);

  D_Flip_Flop d_ff_1 (.D(i_1), .clk(Clock), .Q(O_1), .reset(Reset));  // open: Qn, preset
  D_Flip_Flop d_ff_2 (.D(i_2), .clk(Clock), .Q(O_2), .reset(Reset));  // open: Qn, preset
  D_Flip_Flop d_ff_3 (.D(i_3), .clk(Clock), .Q(O_3), .reset(Reset));  // open: Qn, preset
  D_Flip_Flop d_ff_4 (.D(i_4), .clk(Clock), .Q(O_4), .reset(Reset));  // open: Qn, preset
  D_Flip_Flop d_ff_5 (.D(i_5), .clk(Clock), .Q(O_5), .reset(Reset));  // open: Qn, preset
  D_Flip_Flop d_ff_6 (.D(i_6), .clk(Clock), .Q(O_6), .reset(Reset));  // open: Qn, preset
  D_Flip_Flop d_ff_7 (.D(i_7), .clk(Clock), .Q(O_7), .reset(Reset));  // open: Qn, preset
  D_Flip_Flop d_ff_8 (.D(i_8), .clk(Clock), .Q(O_8), .reset(Reset));  // open: Qn, preset
endmodule

module Full_adder (
  input  C_in,
  input  A,
  input  B,
  output Sum,
  output C_out
);

  wire and_1_out, and_2_out, xor_1_out;

  xor xor_1 (xor_1_out, A, B);
  and and_1 (and_1_out, B, A);
  xor xor_2 (Sum, C_in, xor_1_out);
  and and_2 (and_2_out, xor_1_out, C_in);
  or or_1 (C_out, and_2_out, and_1_out);
endmodule

module Half_adder (
  input  A,
  input  B,
  output Sum,
  output C_out
);

  xor xor_1 (Sum, A, B);
  and and_1 (C_out, B, A);
endmodule

module Eight_bit_adder (
  input  A_1,
  input  B_1,
  input  A_2,
  input  B_2,
  input  A_3,
  input  B_3,
  input  A_4,
  input  B_4,
  input  A_5,
  input  B_5,
  input  A_6,
  input  B_6,
  input  A_7,
  input  B_7,
  input  A_8,
  input  B_8,
  output out_17,
  output out_18,
  output out_19,
  output out_20,
  output out_21,
  output out_22,
  output out_23,
  output out_24,
  output Overflow
);

  wire full_adder_1_c_out, full_adder_2_c_out, full_adder_3_c_out, full_adder_4_c_out, full_adder_5_c_out,
       full_adder_6_c_out, half_adder_1_c_out;

  Half_adder half_adder_1 (.A(A_1), .B(B_1), .Sum(out_17), .C_out(half_adder_1_c_out));
  Full_adder full_adder_1 (.C_in(half_adder_1_c_out), .A(A_2), .B(B_2), .Sum(out_18), .C_out(full_adder_1_c_out));
  Full_adder full_adder_2 (.C_in(full_adder_1_c_out), .A(A_3), .B(B_3), .Sum(out_19), .C_out(full_adder_2_c_out));
  Full_adder full_adder_3 (.C_in(full_adder_2_c_out), .A(A_4), .B(B_4), .Sum(out_20), .C_out(full_adder_3_c_out));
  Full_adder full_adder_4 (.C_in(full_adder_3_c_out), .A(A_5), .B(B_5), .Sum(out_21), .C_out(full_adder_4_c_out));
  Full_adder full_adder_5 (.C_in(full_adder_4_c_out), .A(A_6), .B(B_6), .Sum(out_22), .C_out(full_adder_5_c_out));
  Full_adder full_adder_6 (.C_in(full_adder_5_c_out), .A(A_7), .B(B_7), .Sum(out_23), .C_out(full_adder_6_c_out));
  Full_adder full_adder_7 (.C_in(full_adder_6_c_out), .A(A_8), .B(B_8), .Sum(out_24), .C_out(Overflow));
endmodule

module Calculating_adder (
  input  Reset,
  input  Add,
  input  A_1,
  input  B_1,
  input  A_2,
  input  B_2,
  input  A_3,
  input  B_3,
  input  A_4,
  input  B_4,
  input  A_5,
  input  B_5,
  input  A_6,
  input  B_6,
  input  A_7,
  input  B_7,
  input  A_8,
  input  B_8,
  output out_19,
  output out_20,
  output out_21,
  output out_22,
  output out_23,
  output out_24,
  output out_25,
  output out_26,
  output Overflow
);

  wire eight_bit_adder_1_out_17, eight_bit_adder_1_out_18, eight_bit_adder_1_out_19,
       eight_bit_adder_1_out_20, eight_bit_adder_1_out_21, eight_bit_adder_1_out_22,
       eight_bit_adder_1_out_23, eight_bit_adder_1_out_24, eight_bit_adder_1_overflow;

  Eight_bit_adder eight_bit_adder_1 (
    .A_1(A_1), .B_1(B_1), .A_2(A_2), .B_2(B_2), .A_3(A_3), .B_3(B_3), .A_4(A_4), .B_4(B_4), .A_5(A_5),
    .B_5(B_5), .A_6(A_6), .B_6(B_6), .A_7(A_7), .B_7(B_7), .A_8(A_8), .B_8(B_8),
    .out_17(eight_bit_adder_1_out_17), .out_18(eight_bit_adder_1_out_18), .out_19(eight_bit_adder_1_out_19),
    .out_20(eight_bit_adder_1_out_20), .out_21(eight_bit_adder_1_out_21), .out_22(eight_bit_adder_1_out_22),
    .out_23(eight_bit_adder_1_out_23), .out_24(eight_bit_adder_1_out_24),
    .Overflow(eight_bit_adder_1_overflow));
  Overflow_Register overflow_register_1 (
    .i_1(eight_bit_adder_1_out_17), .i_2(eight_bit_adder_1_out_18), .i_4(eight_bit_adder_1_out_19),
    .i_5(eight_bit_adder_1_out_20), .i_6(eight_bit_adder_1_out_21), .i_7(eight_bit_adder_1_out_22),
    .i_8(eight_bit_adder_1_out_23), .i_9(eight_bit_adder_1_out_24), .i_10(eight_bit_adder_1_overflow),
    .Clock(Add), .Reset(Reset), .out_12(out_19), .out_13(out_20), .out_14(out_21), .out_15(out_22),
    .out_16(out_23), .out_17(out_24), .out_18(out_25), .out_19(out_26), .out_20(Overflow));
endmodule

module Overflow_Register (
  input  i_1,
  input  i_2,
  input  i_4,
  input  i_5,
  input  i_6,
  input  i_7,
  input  i_8,
  input  i_9,
  input  i_10,
  input  Clock,
  input  Reset,
  output out_12,
  output out_13,
  output out_14,
  output out_15,
  output out_16,
  output out_17,
  output out_18,
  output out_19,
  output out_20
);

  D_Flip_Flop d_ff_1 (.D(i_1), .clk(Clock), .Q(out_12), .reset(Reset));  // open: Qn, preset
  D_Flip_Flop d_ff_2 (.D(i_2), .clk(Clock), .Q(out_13), .reset(Reset));  // open: Qn, preset
  D_Flip_Flop d_ff_3 (.D(i_4), .clk(Clock), .Q(out_14), .reset(Reset));  // open: Qn, preset
  D_Flip_Flop d_ff_4 (.D(i_5), .clk(Clock), .Q(out_15), .reset(Reset));  // open: Qn, preset
  D_Flip_Flop d_ff_5 (.D(i_6), .clk(Clock), .Q(out_16), .reset(Reset));  // open: Qn, preset
  D_Flip_Flop d_ff_6 (.D(i_7), .clk(Clock), .Q(out_17), .reset(Reset));  // open: Qn, preset
  D_Flip_Flop d_ff_7 (.D(i_8), .clk(Clock), .Q(out_18), .reset(Reset));  // open: Qn, preset
  D_Flip_Flop d_ff_8 (.D(i_9), .clk(Clock), .Q(out_19), .reset(Reset));  // open: Qn, preset
  D_Flip_Flop d_ff_9 (.D(i_10), .clk(Clock), .Q(out_20), .reset(Reset));  // open: Qn, preset
endmodule
