// Logisim project stage3.circ as structural Verilog: 9 circuits, main circuit interface
module \interface  (
  input  in_1,
  input  in_2,
  input  in_3,
  input  Input_B_Display,
  input  in_5,
  input  in_6,
  input  in_7,
  input  in_8,
  input  in_9,
  input  in_10,
  input  in_11,
  input  Input_B,
  input  in_13,
  input  in_14,
  input  in_15,
  input  in_16,
  input  in_17,
  input  in_18,
  input  in_19,
  input  Input_A,
  input  in_21,
  input  in_22,
  input  in_23,
  input  in_24
);

  wire button_5_out, button_6_out, button_7_out, button_11_out, button_12_out, button_13_out,
       calculating_adder_1_overflow, two_complement_1_pos_or_neg, two_complement_2_pos_or_neg;
  wire [1:0] button_10_out;
  wire [7:0] calculating_adder_1_o_1, custom_register_1_o_1, custom_register_2_o_1, two_complement_1_out_one,
       two_complement_2_out_one;

  Button button_1 ();  // open: out
  LED led_1 ();  // open: in
  LED led_2 ();  // open: in
  Button button_2 ();  // open: out
  Button button_3 ();  // open: out
  Button button_4 ();  // open: out
  LED led_3 ();  // open: in
  Button button_5 (.out(button_5_out));
  LED led_4 ();  // open: in
  LED led_5 ();  // open: in
  LED led_6 (.in(two_complement_1_pos_or_neg));
  LED led_7 ();  // open: in
  LED led_8 ();  // open: in
  Button button_6 (.out(button_6_out));
  Button button_7 (.out(button_7_out));
  LED led_9 (.in(custom_register_1_o_1[7]));
  LED led_10 (.in(custom_register_1_o_1[6]));
  LED led_11 (.in(two_complement_1_out_one[7]));
  LED led_12 (.in(two_complement_1_out_one[6]));
  LED led_13 ();  // open: in
  LED led_14 ();  // open: in
  LED led_15 (.in(custom_register_1_o_1[5]));
  LED led_16 (.in(custom_register_1_o_1[4]));
  LED led_17 (.in(two_complement_1_out_one[5]));
  LED led_18 (.in(two_complement_1_out_one[4]));
  LED led_19 ();  // open: in
  LED led_20 ();  // open: in
  LED led_21 ();  // open: in
  LED led_22 (.in(custom_register_1_o_1[3]));
  LED led_23 (.in(custom_register_1_o_1[2]));
  LED led_24 (.in(two_complement_1_out_one[3]));
  LED led_25 (.in(two_complement_1_out_one[2]));
  Button button_8 ();  // open: out
  LED led_26 ();  // open: in
  LED led_27 ();  // open: in
  LED led_28 ();  // open: in
  Custom_Register custom_register_1 (
    .i_1(in_24), .i_2(in_23), .i_3(in_22), .i_4(in_21), .i_5(Input_A), .i_6(in_19), .i_7(in_18), .i_8(in_17),
    .Clock(button_6_out), .Reset(button_7_out), .O_1(custom_register_1_o_1[0]),
    .O_2(custom_register_1_o_1[1]), .O_3(custom_register_1_o_1[2]), .O_4(custom_register_1_o_1[3]),
    .O_5(custom_register_1_o_1[4]), .O_6(custom_register_1_o_1[5]), .O_7(custom_register_1_o_1[6]),
    .O_8(custom_register_1_o_1[7]));
  LED led_29 (.in(custom_register_1_o_1[1]));
  LED led_30 (.in(custom_register_1_o_1[0]));
  Two_Complement two_complement_1 (
    .Eight(custom_register_1_o_1[7]), .Seven(custom_register_1_o_1[6]), .Six(custom_register_1_o_1[5]),
    .Five(custom_register_1_o_1[4]), .Four(custom_register_1_o_1[3]), .Three(custom_register_1_o_1[2]),
    .Two(custom_register_1_o_1[1]), .One(custom_register_1_o_1[0]), .Toggle(button_5_out),
    .Pos_or_Neg(two_complement_1_pos_or_neg), .Out_One(two_complement_1_out_one[0]),
    .Out_Two(two_complement_1_out_one[1]), .Out_Three(two_complement_1_out_one[2]),
    .Out_Four(two_complement_1_out_one[3]), .Out_Five(two_complement_1_out_one[4]),
    .Out_Six(two_complement_1_out_one[5]), .Out_Seven(two_complement_1_out_one[6]),
    .Out_Eight(two_complement_1_out_one[7]));
  LED led_31 (.in(two_complement_1_out_one[1]));
  LED led_32 (.in(two_complement_1_out_one[0]));
  LED led_33 (.in(calculating_adder_1_o_1[7]));
  LED led_34 ();  // open: in
  LED led_35 ();  // open: in
  LED led_36 (.in(calculating_adder_1_o_1[7]));
  LED led_37 ();  // open: in
  LED led_38 ();  // open: in
  LED led_39 ();  // open: in
  Button button_9 (.out(button_10_out[1]));
  LED led_40 (.in(calculating_adder_1_o_1[6]));
  LED led_41 (.in(calculating_adder_1_o_1[5]));
  LED led_42 ();  // open: in
  LED led_43 ();  // open: in
  LED led_44 ();  // open: in
  Button button_10 (.out(button_10_out[0]));
  LED led_45 (.in(calculating_adder_1_o_1[4]));
  LED led_46 (.in(calculating_adder_1_o_1[3]));
  LED led_47 ();  // open: in
  LED led_48 ();  // open: in
  Button button_11 (.out(button_11_out));
  LED led_49 (.in(two_complement_2_pos_or_neg));
  LED led_50 (.in(calculating_adder_1_o_1[1]));
  LED led_51 (.in(calculating_adder_1_o_1[2]));
  LED led_52 ();  // open: in
  Button button_12 (.out(button_12_out));
  Button button_13 (.out(button_13_out));
  LED led_53 (.in(custom_register_2_o_1[7]));
  LED led_54 (.in(custom_register_2_o_1[6]));
  LED led_55 (.in(two_complement_2_out_one[7]));
  LED led_56 (.in(two_complement_2_out_one[6]));
  Calculating_adder calculating_adder_1 (
    .Reset(button_10_out[0]), .Add(button_10_out[1]), .A_1(two_complement_1_out_one[0]),
    .B_1(two_complement_2_out_one[0]), .A_2(two_complement_1_out_one[1]), .B_2(two_complement_2_out_one[1]),
    .A_3(two_complement_1_out_one[2]), .B_3(two_complement_2_out_one[2]), .A_4(two_complement_1_out_one[3]),
    .B_4(two_complement_2_out_one[3]), .A_5(two_complement_1_out_one[4]), .B_5(two_complement_2_out_one[4]),
    .A_6(two_complement_1_out_one[5]), .B_6(two_complement_2_out_one[5]), .A_7(two_complement_1_out_one[6]),
    .B_7(two_complement_2_out_one[6]), .A_8(two_complement_1_out_one[7]), .B_8(two_complement_2_out_one[7]),
    .O_1(calculating_adder_1_o_1[0]), .O_2(calculating_adder_1_o_1[1]), .O_3(calculating_adder_1_o_1[2]),
    .O_4(calculating_adder_1_o_1[3]), .O_5(calculating_adder_1_o_1[4]), .O_6(calculating_adder_1_o_1[5]),
    .O_7(calculating_adder_1_o_1[6]), .O_8(calculating_adder_1_o_1[7]),
    .Overflow(calculating_adder_1_overflow));
  LED led_57 (.in(calculating_adder_1_o_1[0]));
  LED led_58 ();  // open: in
  LED led_59 (.in(custom_register_2_o_1[5]));
  LED led_60 (.in(custom_register_2_o_1[4]));
  LED led_61 (.in(two_complement_2_out_one[5]));
  LED led_62 (.in(two_complement_2_out_one[4]));
  LED led_63 (.in(custom_register_2_o_1[3]));
  LED led_64 (.in(custom_register_2_o_1[2]));
  LED led_65 (.in(two_complement_2_out_one[3]));
  LED led_66 (.in(two_complement_2_out_one[2]));
  Custom_Register custom_register_2 (
    .i_1(in_16), .i_2(in_15), .i_3(in_14), .i_4(in_13), .i_5(Input_B), .i_6(in_11), .i_7(in_10), .i_8(in_9),
    .Clock(button_12_out), .Reset(button_13_out), .O_1(custom_register_2_o_1[0]),
    .O_2(custom_register_2_o_1[1]), .O_3(custom_register_2_o_1[2]), .O_4(custom_register_2_o_1[3]),
    .O_5(custom_register_2_o_1[4]), .O_6(custom_register_2_o_1[5]), .O_7(custom_register_2_o_1[6]),
    .O_8(custom_register_2_o_1[7]));
  LED led_67 (.in(custom_register_2_o_1[1]));
  LED led_68 (.in(custom_register_2_o_1[0]));
  Two_Complement two_complement_2 (
    .Eight(custom_register_2_o_1[7]), .Seven(custom_register_2_o_1[6]), .Six(custom_register_2_o_1[5]),
    .Five(custom_register_2_o_1[4]), .Four(custom_register_2_o_1[3]), .Three(custom_register_2_o_1[2]),
    .Two(custom_register_2_o_1[1]), .One(custom_register_2_o_1[0]), .Toggle(button_11_out),
    .Pos_or_Neg(two_complement_2_pos_or_neg), .Out_One(two_complement_2_out_one[0]),
    .Out_Two(two_complement_2_out_one[1]), .Out_Three(two_complement_2_out_one[2]),
    .Out_Four(two_complement_2_out_one[3]), .Out_Five(two_complement_2_out_one[4]),
    .Out_Six(two_complement_2_out_one[5]), .Out_Seven(two_complement_2_out_one[6]),
    .Out_Eight(two_complement_2_out_one[7]));
  LED led_69 (.in(two_complement_2_out_one[1]));
  LED led_70 (.in(two_complement_2_out_one[0]));

  // Notes on the sheet:
  //   +/-
  //   +/-
  //   Load
  //   Subtract
  //   Reset
  //   +/-
  //   +/-
  //   Load
  //   Reset
  //   Input A Display
  //   +/-
  //   8 bit Binary Calculator
  //   +/-
  //   +/-
  //   +/-
  //   Output
  //   Add
  //   Reset
  //   +/-
  //   Input B
  //   +/-
  //   Load
  //   Reset
endmodule

module Custom_Register (
  input  i_1,
  input  i_2,
  input  i_3,
  input  i_4,
  input  i_5,
  input  i_6,
  input  i_7,
  input  i_8,
  input  Clock,
  input  Reset,
  output O_1,
  output O_2,
  output O_3,
  output O_4,
  output O_5,
  output O_6,
  output O_7,
  output O_8
);

  D_Flip_Flop d_ff_1 (.D(i_1), .clk(Clock), .Q(O_1), .reset(Reset));  // open: Qn, preset
  D_Flip_Flop d_ff_2 (.D(i_2), .clk(Clock), .Q(O_2), .reset(Reset));  // open: Qn, preset
  D_Flip_Flop d_ff_3 (.D(i_3), .clk(Clock), .Q(O_3), .reset(Reset));  // open: Qn, preset
  D_Flip_Flop d_ff_4 (.D(i_4), .clk(Clock), .Q(O_4), .reset(Reset));  // open: Qn, preset
  D_Flip_Flop d_ff_5 (.D(i_5), .clk(Clock), .Q(O_5), .reset(Reset));  // open: Qn, preset
  D_Flip_Flop d_ff_6 (.D(i_6), .clk(Clock), .Q(O_6), .reset(Reset));  // open: Qn, preset
  D_Flip_Flop d_ff_7 (.D(i_7), .clk(Clock), .Q(O_7), .reset(Reset));  // open: Qn, preset
  D_Flip_Flop d_ff_8 (.D(i_8), .clk(Clock), .Q(O_8), .reset(Reset));  // open: Qn, preset
endmodule

module Full_adder (
  input  C_in,
  input  A,
  input  B,
  output Sum,
  output C_out
);

  wire and_1_out, and_2_out, xor_1_out;

  xor xor_1 (xor_1_out, A, B);
  and and_1 (and_1_out, B, A);
  xor xor_2 (Sum, C_in, xor_1_out);
  and and_2 (and_2_out, xor_1_out, C_in);
  or or_1 (C_out, and_2_out, and_1_out);
endmodule

module Half_adder (
  input  A,
  input  B,
  output Sum,
  output C_out
);

  xor xor_1 (Sum, A, B);
  and and_1 (C_out, B, A);
endmodule

module Eight_bit_adder (
  input  A_1,
  input  B_1,
  input  A_2,
  input  B_2,
  input  A_3,
  input  B_3,
  input  A_4,
  input  B_4,
  input  A_5,
  input  B_5,
  input  A_6,
  input  B_6,
  input  A_7,
  input  B_7,
  input  A_8,
  input  B_8,
  output O_1,
  output O_2,
  output O_3,
  output O_4,
  output O_5,
  output O_6,
  output O_7,
  output O_8,
  output Overflow
);

  wire full_adder_1_c_out, full_adder_2_c_out, full_adder_3_c_out, full_adder_4_c_out, full_adder_5_c_out,
       full_adder_6_c_out, full_adder_7_c_out;

  Full_adder full_adder_1 (.A(A_1), .B(B_1), .Sum(O_1), .C_out(full_adder_1_c_out));  // open: C_in
  Full_adder full_adder_2 (.C_in(full_adder_1_c_out), .A(A_2), .B(B_2), .Sum(O_2), .C_out(full_adder_2_c_out));
  Full_adder full_adder_3 (.C_in(full_adder_2_c_out), .A(A_3), .B(B_3), .Sum(O_3), .C_out(full_adder_3_c_out));
  Full_adder full_adder_4 (.C_in(full_adder_3_c_out), .A(A_4), .B(B_4), .Sum(O_4), .C_out(full_adder_4_c_out));
  Full_adder full_adder_5 (.C_in(full_adder_4_c_out), .A(A_5), .B(B_5), .Sum(O_5), .C_out(full_adder_5_c_out));
  Full_adder full_adder_6 (.C_in(full_adder_5_c_out), .A(A_6), .B(B_6), .Sum(O_6), .C_out(full_adder_6_c_out));
  Full_adder full_adder_7 (.C_in(full_adder_6_c_out), .A(A_7), .B(B_7), .Sum(O_7), .C_out(full_adder_7_c_out));
  Full_adder full_adder_8 (.C_in(full_adder_7_c_out), .A(A_8), .B(B_8), .Sum(O_8), .C_out(Overflow));
endmodule

module Calculating_adder (
  input  Reset,
  input  Add,
  input  A_1,
  input  B_1,
  input  A_2,
  input  B_2,
  input  A_3,
  input  B_3,
  input  A_4,
  input  B_4,
  input  A_5,
  input  B_5,
  input  A_6,
  input  B_6,
  input  A_7,
  input  B_7,
  input  A_8,
  input  B_8,
  output O_1,
  output O_2,
  output O_3,
  output O_4,
  output O_5,
  output O_6,
  output O_7,
  output O_8,
  output Overflow
);

  wire eight_bit_adder_1_o_1, eight_bit_adder_1_o_2, eight_bit_adder_1_o_3, eight_bit_adder_1_o_4,
       eight_bit_adder_1_o_5, eight_bit_adder_1_o_6, eight_bit_adder_1_o_7, eight_bit_adder_1_o_8,
       eight_bit_adder_1_overflow;

  Eight_bit_adder eight_bit_adder_1 (
    .A_1(A_1), .B_1(B_1), .A_2(A_2), .B_2(B_2), .A_3(A_3), .B_3(B_3), .A_4(A_4), .B_4(B_4), .A_5(A_5),
    .B_5(B_5), .A_6(A_6), .B_6(B_6), .A_7(A_7), .B_7(B_7), .A_8(A_8), .B_8(B_8), .O_1(eight_bit_adder_1_o_1),
    .O_2(eight_bit_adder_1_o_2), .O_3(eight_bit_adder_1_o_3), .O_4(eight_bit_adder_1_o_4),
    .O_5(eight_bit_adder_1_o_5), .O_6(eight_bit_adder_1_o_6), .O_7(eight_bit_adder_1_o_7),
    .O_8(eight_bit_adder_1_o_8), .Overflow(eight_bit_adder_1_overflow));
  Overflow_Register overflow_register_1 (
    .i_1(eight_bit_adder_1_o_1), .i_2(eight_bit_adder_1_o_2), .i_4(eight_bit_adder_1_o_3),
    .i_5(eight_bit_adder_1_o_4), .i_6(eight_bit_adder_1_o_5), .i_7(eight_bit_adder_1_o_6),
    .i_8(eight_bit_adder_1_o_7), .i_9(eight_bit_adder_1_o_8), .i_10(eight_bit_adder_1_overflow), .Clock(Add),
    .Reset(Reset), .out_12(O_1), .out_13(O_2), .out_14(O_3), .out_15(O_4), .out_16(O_5), .out_17(O_6),
    .out_18(O_7), .out_19(O_8), .out_20(Overflow));
endmodule

module Overflow_Register (
  input  i_1,
  input  i_2,
  input  i_4,
  input  i_5,
  input  i_6,
  input  i_7,
  input  i_8,
  input  i_9,
  input  i_10,
  input  Clock,
  input  Reset,
  output out_12,
  output out_13,
  output out_14,
  output out_15,
  output out_16,
  output out_17,
  output out_18,
  output out_19,
  output out_20
);

  D_Flip_Flop d_ff_1 (.D(i_1), .clk(Clock), .Q(out_12), .reset(Reset));  // open: Qn, preset
  D_Flip_Flop d_ff_2 (.D(i_2), .clk(Clock), .Q(out_13), .reset(Reset));  // open: Qn, preset
  D_Flip_Flop d_ff_3 (.D(i_4), .clk(Clock), .Q(out_14), .reset(Reset));  // open: Qn, preset
  D_Flip_Flop d_ff_4 (.D(i_5), .clk(Clock), .Q(out_15), .reset(Reset));  // open: Qn, preset
  D_Flip_Flop d_ff_5 (.D(i_6), .clk(Clock), .Q(out_16), .reset(Reset));  // open: Qn, preset
  D_Flip_Flop d_ff_6 (.D(i_7), .clk(Clock), .Q(out_17), .reset(Reset));  // open: Qn, preset
  D_Flip_Flop d_ff_7 (.D(i_8), .clk(Clock), .Q(out_18), .reset(Reset));  // open: Qn, preset
  D_Flip_Flop d_ff_8 (.D(i_9), .clk(Clock), .Q(out_19), .reset(Reset));  // open: Qn, preset
  D_Flip_Flop d_ff_9 (.D(i_10), .clk(Clock), .Q(out_20), .reset(Reset));  // open: Qn, preset
endmodule

module draft (
  input  in_1,
  input  in_2,
  input  in_3,
  input  Input_A,
  input  in_5,
  input  in_6,
  input  in_7,
  input  in_8
);

  wire button_1_out, button_2_out, button_3_out, custom_register_1_o_1, custom_register_1_o_2,
       custom_register_1_o_3, custom_register_1_o_4, custom_register_1_o_5, custom_register_1_o_6,
       custom_register_1_o_7, custom_register_1_o_8, j_k_ff_1_q, j_k_ff_1_qn, or_1_out, or_2_out, or_3_out,
       or_4_out, or_5_out, or_6_out, or_7_out, or_8_out, or_9_out, or_10_out, or_11_out, or_12_out,
       or_13_out, or_14_out, or_15_out, or_16_out;
  wire [7:0] and_8_out, and_16_out, two_complement_1_out_one, two_complement_2_out_one;

  or or_1 (or_1_out, two_complement_1_out_one[6], and_8_out[7]);
  LED led_1 (.in(or_1_out));
  or or_2 (or_2_out, two_complement_1_out_one[6], and_8_out[6]);
  LED led_2 (.in(or_2_out));
  or or_3 (or_3_out, two_complement_1_out_one[5], and_8_out[5]);
  LED led_3 (.in(or_3_out));
  or or_4 (or_4_out, two_complement_1_out_one[4], and_8_out[4]);
  LED led_4 (.in(or_4_out));
  or or_5 (or_5_out, two_complement_1_out_one[3], and_8_out[3]);
  LED led_5 (.in(or_5_out));
  or or_6 (or_6_out, two_complement_1_out_one[2], and_8_out[2]);
  LED led_6 (.in(or_6_out));
  or or_7 (or_7_out, two_complement_1_out_one[1], and_8_out[1]);
  LED led_7 (.in(or_7_out));
  or or_8 (or_8_out, two_complement_1_out_one[0], and_8_out[0]);
  LED led_8 (.in(or_8_out));
  and and_1 (and_8_out[7], custom_register_1_o_8, j_k_ff_1_qn);
  and and_2 (and_8_out[6], custom_register_1_o_7, j_k_ff_1_qn);
  and and_3 (and_8_out[5], custom_register_1_o_6, j_k_ff_1_qn);
  LED led_9 (.in(j_k_ff_1_q));
  and and_4 (and_8_out[4], custom_register_1_o_5, j_k_ff_1_qn);
  and and_5 (and_8_out[3], custom_register_1_o_4, j_k_ff_1_qn);
  or or_9 (or_9_out, and_8_out[7], two_complement_2_out_one[7]);
  LED led_10 (.in(or_9_out));
  and and_6 (and_8_out[2], custom_register_1_o_3, j_k_ff_1_qn);
  and and_7 (and_8_out[1], custom_register_1_o_2, j_k_ff_1_qn);
  or or_10 (or_10_out, and_8_out[6], two_complement_2_out_one[6]);
  LED led_11 (.in(or_10_out));
  and and_8 (and_8_out[0], custom_register_1_o_1, j_k_ff_1_qn);
  or or_11 (or_11_out, and_8_out[5], two_complement_2_out_one[5]);
  LED led_12 (.in(or_11_out));
  Button button_1 (.out(button_1_out));
  or or_12 (or_12_out, and_8_out[4], two_complement_2_out_one[4]);
  LED led_13 (.in(or_12_out));
  J_K_Flip_Flop j_k_ff_1 (
    .J(1'b1), .K(1'b1), .clk(button_1_out), .Q(j_k_ff_1_q), .Qn(j_k_ff_1_qn));  // open: preset, reset
  or or_13 (or_13_out, and_8_out[3], two_complement_2_out_one[3]);
  LED led_14 (.in(or_13_out));
  LED led_15 (.in(j_k_ff_1_q));
  or or_14 (or_14_out, and_8_out[2], two_complement_2_out_one[2]);
  LED led_16 (.in(or_14_out));
  Button button_2 (.out(button_2_out));
  Button button_3 (.out(button_3_out));
  and and_9 (and_16_out[7], j_k_ff_1_q, custom_register_1_o_8);
  and and_10 (and_16_out[6], j_k_ff_1_q, custom_register_1_o_7);
  or or_15 (or_15_out, and_8_out[1], two_complement_2_out_one[1]);
  LED led_17 (.in(or_15_out));
  and and_11 (and_16_out[5], j_k_ff_1_q, custom_register_1_o_6);
  and and_12 (and_16_out[4], j_k_ff_1_q, custom_register_1_o_5);
  or or_16 (or_16_out, and_8_out[0], two_complement_2_out_one[0]);
  LED led_18 (.in(or_16_out));
  and and_13 (and_16_out[3], j_k_ff_1_q, custom_register_1_o_4);
  and and_14 (and_16_out[2], j_k_ff_1_q, custom_register_1_o_3);
  Custom_Register custom_register_1 (
    .i_1(in_8), .i_2(in_7), .i_3(in_6), .i_4(in_5), .i_5(Input_A), .i_6(in_3), .i_7(in_2), .i_8(in_1),
    .Clock(button_2_out), .Reset(button_3_out), .O_1(custom_register_1_o_1), .O_2(custom_register_1_o_2),
    .O_3(custom_register_1_o_3), .O_4(custom_register_1_o_4), .O_5(custom_register_1_o_5),
    .O_6(custom_register_1_o_6), .O_7(custom_register_1_o_7), .O_8(custom_register_1_o_8));
  and and_15 (and_16_out[1], j_k_ff_1_q, custom_register_1_o_2);
  and and_16 (and_16_out[0], j_k_ff_1_q, custom_register_1_o_1);
  Two_Complement two_complement_1 (
    .Eight(and_16_out[7]), .Seven(and_16_out[6]), .Six(and_16_out[5]), .Five(and_16_out[4]),
    .Four(and_16_out[3]), .Three(and_16_out[2]), .Two(and_16_out[1]), .One(and_16_out[0]), .Toggle(1'b1),
    .Out_One(two_complement_1_out_one[0]), .Out_Two(two_complement_1_out_one[1]),
    .Out_Three(two_complement_1_out_one[2]), .Out_Four(two_complement_1_out_one[3]),
    .Out_Five(two_complement_1_out_one[4]), .Out_Six(two_complement_1_out_one[5]),
    .Out_Seven(two_complement_1_out_one[6]), .Out_Eight(two_complement_1_out_one[7]));  // open: Pos_or_Neg
  Two_Complement two_complement_2 (
    .Eight(two_complement_1_out_one[7]), .Seven(two_complement_1_out_one[6]),
    .Six(two_complement_1_out_one[5]), .Five(two_complement_1_out_one[4]),
    .Four(two_complement_1_out_one[3]), .Three(two_complement_1_out_one[2]),
    .Two(two_complement_1_out_one[1]), .One(two_complement_1_out_one[0]), .Toggle(1'b1),
    .Out_One(two_complement_2_out_one[0]), .Out_Two(two_complement_2_out_one[1]),
    .Out_Three(two_complement_2_out_one[2]), .Out_Four(two_complement_2_out_one[3]),
    .Out_Five(two_complement_2_out_one[4]), .Out_Six(two_complement_2_out_one[5]),
    .Out_Seven(two_complement_2_out_one[6]), .Out_Eight(two_complement_2_out_one[7]));  // open: Pos_or_Neg

  // Notes on the sheet:
  //   +/-
  //   +/-
  //   +/-
  //   Load
  //   Reset
endmodule

module Two_Complement (
  input  Eight,
  input  Seven,
  input  Six,
  input  Five,
  input  Four,
  input  Three,
  input  Two,
  input  One,
  input  Toggle,
  output Pos_or_Neg,
  output Out_One,
  output Out_Two,
  output Out_Three,
  output Out_Four,
  output Out_Five,
  output Out_Six,
  output Out_Seven,
  output Out_Eight
);

  wire [7:0] xor_8_out;

  J_K_Flip_Flop j_k_ff_1 (.J(1'b1), .K(1'b1), .clk(Toggle), .Q(Pos_or_Neg));  // open: Qn, preset, reset
  xor xor_1 (xor_8_out[7], Pos_or_Neg, Eight);
  xor xor_2 (xor_8_out[6], Pos_or_Neg, Seven);
  xor xor_3 (xor_8_out[5], Pos_or_Neg, Six);
  xor xor_4 (xor_8_out[4], Pos_or_Neg, Five);
  xor xor_5 (xor_8_out[3], Pos_or_Neg, Four);
  xor xor_6 (xor_8_out[2], Pos_or_Neg, Three);
  xor xor_7 (xor_8_out[1], Pos_or_Neg, Two);
  Eight_bit_adder eight_bit_adder_1 (
    .A_1(xor_8_out[0]), .B_1(Pos_or_Neg), .A_2(xor_8_out[1]), .A_3(xor_8_out[2]), .A_4(xor_8_out[3]),
    .A_5(xor_8_out[4]), .A_6(xor_8_out[5]), .A_7(xor_8_out[6]), .A_8(xor_8_out[7]), .O_1(Out_One),
    .O_2(Out_Two), .O_3(Out_Three), .O_4(Out_Four), .O_5(Out_Five), .O_6(Out_Six), .O_7(Out_Seven),
    .O_8(Out_Eight));  // open: B_2, B_3, B_4, B_5, B_6, B_7, B_8, Overflow
  xor xor_8 (xor_8_out[0], Pos_or_Neg, One);
endmodule
