// Logisim project stage2.circ as structural Verilog: 4 circuits, main circuit interface
module \interface  (
  input  A7,
  input  A6,
  input  A5,
  input  A4,
  input  A3,
  input  A2,
  input  A1,
  input  A0,
  input  B7,
  input  B6,
  input  B5,
  input  B4,
  input  B3,
  input  B2,
  input  B1,
  input  B0
);

  wire button_1_out, button_2_out, button_3_out, button_4_out, button_5_out, button_6_out,
       eight_bit_adder_1_out_3, eight_bit_adder_1_out_4, eight_bit_adder_1_out_5, eight_bit_adder_1_out_6,
       eight_bit_adder_1_out_7, eight_bit_adder_1_out_8, eight_bit_adder_1_out_9, eight_bit_adder_1_out_10,
       eight_bit_register_3_out_11, eight_bit_register_3_out_12, eight_bit_register_3_out_13,
       eight_bit_register_3_out_14, eight_bit_register_3_out_15, eight_bit_register_3_out_16,
       eight_bit_register_3_out_17, eight_bit_register_3_out_18;
  wire [7:0] eight_bit_register_1_out_11, eight_bit_register_2_out_11;

  Button button_1 (.out(button_1_out));
  Button button_2 (.out(button_2_out));
  LED led_1 (.in(eight_bit_register_1_out_11[7]));
  LED led_2 (.in(eight_bit_register_1_out_11[6]));
  LED led_3 (.in(eight_bit_register_1_out_11[5]));
  LED led_4 (.in(eight_bit_register_1_out_11[4]));
  LED led_5 (.in(eight_bit_register_1_out_11[3]));
  LED led_6 (.in(eight_bit_register_1_out_11[2]));
  LED led_7 (.in(eight_bit_register_1_out_11[1]));
  LED led_8 (.in(eight_bit_register_1_out_11[0]));
  eight_bit_register eight_bit_register_1 (
    .in_1(A0), .in_2(A1), .in_3(A2), .in_4(A3), .in_5(A4), .in_6(A5), .in_7(A6), .in_8(A7),
    .load(button_2_out), .reset(button_1_out), .out_11(eight_bit_register_1_out_11[0]),
    .out_12(eight_bit_register_1_out_11[1]), .out_13(eight_bit_register_1_out_11[2]),
    .out_14(eight_bit_register_1_out_11[3]), .out_15(eight_bit_register_1_out_11[4]),
    .out_16(eight_bit_register_1_out_11[5]), .out_17(eight_bit_register_1_out_11[6]),
    .out_18(eight_bit_register_1_out_11[7]));
  Button button_3 (.out(button_3_out));
  Button button_4 (.out(button_4_out));
  LED led_9 (.in(eight_bit_register_2_out_11[7]));
  LED led_10 (.in(eight_bit_register_2_out_11[6]));
  LED led_11 (.in(eight_bit_register_2_out_11[5]));
  LED led_12 (.in(eight_bit_register_2_out_11[4]));
  LED led_13 (.in(eight_bit_register_2_out_11[3]));
  LED led_14 (.in(eight_bit_register_2_out_11[2]));
  LED led_15 (.in(eight_bit_register_2_out_11[1]));
  LED led_16 (.in(eight_bit_register_2_out_11[0]));
  eight_bit_register eight_bit_register_2 (
    .in_1(B0), .in_2(B1), .in_3(B2), .in_4(B3), .in_5(B4), .in_6(B5), .in_7(B6), .in_8(B7),
    .load(button_4_out), .reset(button_3_out), .out_11(eight_bit_register_2_out_11[0]),
    .out_12(eight_bit_register_2_out_11[1]), .out_13(eight_bit_register_2_out_11[2]),
    .out_14(eight_bit_register_2_out_11[3]), .out_15(eight_bit_register_2_out_11[4]),
    .out_16(eight_bit_register_2_out_11[5]), .out_17(eight_bit_register_2_out_11[6]),
    .out_18(eight_bit_register_2_out_11[7]));
  eight_bit_adder eight_bit_adder_1 (
    .A(eight_bit_register_1_out_11), .B(eight_bit_register_2_out_11), .out_3(eight_bit_adder_1_out_3),
    .out_4(eight_bit_adder_1_out_4), .out_5(eight_bit_adder_1_out_5), .out_6(eight_bit_adder_1_out_6),
    .out_7(eight_bit_adder_1_out_7), .out_8(eight_bit_adder_1_out_8), .out_9(eight_bit_adder_1_out_9),
    .out_10(eight_bit_adder_1_out_10));
  Button button_5 (.out(button_5_out));
  Button button_6 (.out(button_6_out));
  LED led_17 (.in(eight_bit_register_3_out_11));
  eight_bit_register eight_bit_register_3 (
    .in_1(eight_bit_adder_1_out_3), .in_2(eight_bit_adder_1_out_4), .in_3(eight_bit_adder_1_out_5),
    .in_4(eight_bit_adder_1_out_6), .in_5(eight_bit_adder_1_out_7), .in_6(eight_bit_adder_1_out_8),
    .in_7(eight_bit_adder_1_out_9), .in_8(eight_bit_adder_1_out_10), .load(button_5_out),
    .reset(button_6_out), .out_11(eight_bit_register_3_out_11), .out_12(eight_bit_register_3_out_12),
    .out_13(eight_bit_register_3_out_13), .out_14(eight_bit_register_3_out_14),
    .out_15(eight_bit_register_3_out_15), .out_16(eight_bit_register_3_out_16),
    .out_17(eight_bit_register_3_out_17), .out_18(eight_bit_register_3_out_18));
  LED led_18 (.in(eight_bit_register_3_out_12));
  LED led_19 (.in(eight_bit_register_3_out_13));
  LED led_20 (.in(eight_bit_register_3_out_14));
  LED led_21 (.in(eight_bit_register_3_out_15));
  LED led_22 (.in(eight_bit_register_3_out_16));
  LED led_23 (.in(eight_bit_register_3_out_17));
  LED led_24 (.in(eight_bit_register_3_out_18));

  // Notes on the sheet:
  //   Input A
  //   8 bit Binary Calculator
  //   Input B
endmodule

module full_adder (
  input  Cin,
  input  A,
  input  B,
  output Sum,
  output Cout
);

  wire and_1_out, and_2_out, xor_1_out;

  xor xor_1 (xor_1_out, A, B);
  and and_1 (and_1_out, B, A);
  xor xor_2 (Sum, xor_1_out, Cin);
  and and_2 (and_2_out, xor_1_out, Cin);
  or or_1 (Cout, and_2_out, and_1_out);
endmodule

module eight_bit_register (
  input  in_1,
  input  in_2,
  input  in_3,
  input  in_4,
  input  in_5,
  input  in_6,
  input  in_7,
  input  in_8,
  input  load,
  input  reset,
  output out_11,
  output out_12,
  output out_13,
  output out_14,
  output out_15,
  output out_16,
  output out_17,
  output out_18
);

  D_Flip_Flop d_ff_1 (.D(in_1), .clk(load), .Q(out_11), .reset(reset));  // open: Qn, preset
  D_Flip_Flop d_ff_2 (.D(in_2), .clk(load), .Q(out_12), .reset(reset));  // open: Qn, preset
  D_Flip_Flop d_ff_3 (.D(in_3), .clk(load), .Q(out_13), .reset(reset));  // open: Qn, preset
  D_Flip_Flop d_ff_4 (.D(in_4), .clk(load), .Q(out_14), .reset(reset));  // open: Qn, preset
  D_Flip_Flop d_ff_5 (.D(in_5), .clk(load), .Q(out_15), .reset(reset));  // open: Qn, preset
  D_Flip_Flop d_ff_6 (.D(in_6), .clk(load), .Q(out_16), .reset(reset));  // open: Qn, preset
  D_Flip_Flop d_ff_7 (.D(in_7), .clk(load), .Q(out_17), .reset(reset));  // open: Qn, preset
  D_Flip_Flop d_ff_8 (.D(in_8), .clk(load), .Q(out_18), .reset(reset));  // open: Qn, preset
endmodule

module eight_bit_adder (
  input  [7:0] A,
  input  [7:0] B,
  output out_3,
  output out_4,
  output out_5,
  output out_6,
  output out_7,
  output out_8,
  output out_9,
  output out_10
);

  wire and_1_out, and_2_out, and_3_out, and_4_out, and_5_out, and_6_out, and_7_out, and_8_out, and_9_out,
       and_10_out, and_11_out, and_12_out, and_13_out, and_14_out, and_15_out, or_1_out, or_2_out, or_3_out,
       or_4_out, or_5_out, or_6_out, xor_1_out, xor_2_out, xor_3_out, xor_4_out, xor_5_out, xor_6_out,
       xor_7_out;

  xor xor_1 (xor_1_out, A[1], B[1]);
  and and_1 (and_1_out, B[1], A[1]);
  xor xor_2 (xor_2_out, A[2], B[2]);
  and and_2 (and_2_out, B[2], A[2]);
  xor xor_3 (xor_3_out, A[3], B[3]);
  and and_3 (and_3_out, B[3], A[3]);
  xor xor_4 (xor_4_out, A[4], B[4]);
  and and_4 (and_4_out, B[4], A[4]);
  xor xor_5 (xor_5_out, A[5], B[5]);
  and and_5 (and_5_out, B[5], A[5]);
  xor xor_6 (xor_6_out, A[6], B[6]);
  and and_6 (and_6_out, B[6], A[6]);
  xor xor_7 (xor_7_out, A[7], B[7]);
  and and_7 (and_7_out, B[7], A[7]);
  xor xor_8 (out_3, A[0], B[0]);
  and and_8 (and_8_out, B[0], A[0]);
  xor xor_9 (out_4, xor_1_out, and_8_out);
  and and_9 (and_9_out, xor_1_out, and_8_out);
  xor xor_10 (out_5, xor_2_out, or_1_out);
  and and_10 (and_10_out, xor_2_out, or_1_out);
  xor xor_11 (out_6, xor_3_out, or_2_out);
  and and_11 (and_11_out, xor_3_out, or_2_out);
  xor xor_12 (out_7, xor_4_out, or_3_out);
  and and_12 (and_12_out, xor_4_out, or_3_out);
  xor xor_13 (out_8, xor_5_out, or_4_out);
  and and_13 (and_13_out, xor_5_out, or_4_out);
  xor xor_14 (out_9, xor_6_out, or_5_out);
  and and_14 (and_14_out, xor_6_out, or_5_out);
  xor xor_15 (out_10, xor_7_out, or_6_out);
  and and_15 (and_15_out, xor_7_out, or_6_out);
  or or_1 (or_1_out, and_1_out, and_9_out);
  or or_2 (or_2_out, and_2_out, and_10_out);
  or or_3 (or_3_out, and_3_out, and_11_out);
  or or_4 (or_4_out, and_4_out, and_12_out);
  or or_5 (or_5_out, and_5_out, and_13_out);
  or or_6 (or_6_out, and_6_out, and_14_out);
  // OR_Gate or_7 has open pins: in0=and_7_out, in1=and_15_out, out=open
endmodule
