// Logisim project Lab01.circ as structural Verilog: 1 circuit, main circuit main
module main (
  input  _8,
  input  in_2,
  input  in_3,
  input  _13,
  input  in_5,
  input  _15,
  input  in_7,
  input  in_8
);

  wire and_1_out, and_2_out, and_3_out, and_4_out, not_1_out, not_2_out, not_3_out, not_4_out, not_5_out,
       not_6_out, or_1_out, or_2_out, xor_1_out;

  not not_1 (not_1_out, _8);
  xor xor_1 (xor_1_out, in_2, in_3);
  not not_2 (not_2_out, in_5);
  not not_3 (not_3_out, _13);
  not not_4 (not_4_out, _15);
  not not_5 (not_5_out, in_7);
  not not_6 (not_6_out, in_8);
  LED led_1 (.in(not_1_out));
  LED led_2 (.in(xor_1_out));
  and and_1 (and_1_out, _15, in_7, in_8);
  and and_2 (and_2_out, not_4_out, not_5_out, not_6_out);
  and and_3 (and_3_out, _13, in_5);
  and and_4 (and_4_out, not_2_out, not_3_out);
  or or_1 (or_1_out, and_3_out, and_4_out);
  LED led_3 (.in(or_1_out));
  or or_2 (or_2_out, and_1_out, and_2_out);
  LED led_4 (.in(or_2_out));

  // Notes on the sheet:
  //   10.
endmodule
