// Logisim project Lab02.circ as structural Verilog: 3 circuits, main circuit FullAdder
module FullAdder (
  input  A,
  input  B,
  input  C_in,
  output Sum,
  output C_out
);

  wire and_1_out, and_2_out, xor_1_out, xor_2_out;

  xor xor_1 (xor_1_out, A, B);
  xor xor_2 (xor_2_out, B, A);
  xor xor_3 (Sum, xor_1_out, C_in);
  and and_1 (and_1_out, xor_2_out, C_in);
  and and_2 (and_2_out, B, A);
  or or_1 (C_out, and_1_out, and_2_out);
endmodule

module HalfAdder (
  input  A,
  input  B,
  output C_out,
  output Sum,
  output out_5
);

  wire and_2_out, and_3_out, not_1_out, not_2_out;

  not not_1 (not_1_out, A);
  not not_2 (not_2_out, B);
  and and_1 (C_out, B, A);
  and and_2 (and_2_out, not_1_out, B);
  and and_3 (and_3_out, not_2_out, A);
  or or_1 (Sum, and_2_out, and_3_out);
endmodule

module Main (
  input  A_4,
  input  B_4,
  input  A_3,
  input  B_3,
  input  A_2,
  input  B_2,
  input  A_1,
  input  B_1,
  input  A_8,
  input  B_8,
  input  A_7,
  input  B_7,
  input  A_6,
  input  B_6,
  input  A_5,
  input  B_5
);

  wire and_1_out, and_2_out, and_3_out, and_4_out, and_5_out, and_6_out, and_7_out, and_8_out, and_9_out,
       fulladder_1_c_out, fulladder_1_sum, fulladder_2_c_out, fulladder_2_sum, fulladder_3_c_out,
       fulladder_3_sum, halfadder_1_c_out, halfadder_1_sum, not_1_out, not_2_out, or_1_out, or_2_out,
       or_3_out, or_4_out, xor_1_out, xor_2_out, xor_3_out, xor_4_out, xor_5_out, xor_6_out, xor_7_out,
       xor_8_out, xor_9_out;

  HalfAdder halfadder_1 (.A(A_4), .B(B_4), .C_out(halfadder_1_c_out), .Sum(halfadder_1_sum));  // open: out_5
  FullAdder fulladder_1 (.A(A_3), .B(B_3), .C_in(halfadder_1_c_out), .Sum(fulladder_1_sum), .C_out(fulladder_1_c_out));
  FullAdder fulladder_2 (.A(A_2), .B(B_2), .C_in(fulladder_1_c_out), .Sum(fulladder_2_sum), .C_out(fulladder_2_c_out));
  FullAdder fulladder_3 (.A(A_1), .B(B_1), .C_in(fulladder_2_c_out), .Sum(fulladder_3_sum), .C_out(fulladder_3_c_out));
  LED led_1 (.in(halfadder_1_sum));
  LED led_2 (.in(fulladder_1_sum));
  LED led_3 (.in(fulladder_2_sum));
  LED led_4 (.in(fulladder_3_sum));
  LED led_5 (.in(fulladder_3_c_out));
  not not_1 (not_1_out, A_8);
  not not_2 (not_2_out, B_8);
  xor xor_1 (xor_1_out, A_7, B_7);
  xor xor_2 (xor_2_out, A_6, B_6);
  xor xor_3 (xor_3_out, A_5, B_5);
  xor xor_4 (xor_4_out, B_7, A_7);
  xor xor_5 (xor_5_out, B_6, A_6);
  xor xor_6 (xor_6_out, B_5, A_5);
  and and_1 (and_1_out, B_8, A_8);
  and and_2 (and_2_out, not_1_out, B_8);
  and and_3 (and_3_out, not_2_out, A_8);
  xor xor_7 (xor_7_out, xor_1_out, and_1_out);
  and and_4 (and_4_out, xor_4_out, and_1_out);
  and and_5 (and_5_out, B_7, A_7);
  xor xor_8 (xor_8_out, xor_2_out, or_2_out);
  and and_6 (and_6_out, xor_5_out, or_2_out);
  and and_7 (and_7_out, B_6, A_6);
  xor xor_9 (xor_9_out, xor_3_out, or_3_out);
  and and_8 (and_8_out, xor_6_out, or_3_out);
  and and_9 (and_9_out, B_5, A_5);
  or or_1 (or_1_out, and_2_out, and_3_out);
  LED led_6 (.in(xor_7_out));
  LED led_7 (.in(xor_8_out));
  LED led_8 (.in(xor_9_out));
  LED led_9 (.in(or_1_out));
  or or_2 (or_2_out, and_4_out, and_5_out);
  or or_3 (or_3_out, and_6_out, and_7_out);
  or or_4 (or_4_out, and_8_out, and_9_out);
  LED led_10 (.in(or_4_out));
endmodule
