// Logisim project lab03.circ as structural Verilog: 1 circuit, main circuit main
module main (
  input  Set,
  input  Reset,
  input  S,
  input  Re_set,
  input  s_et,
  input  J,
  input  K,
  input  in_8,
  input  in_9,
  input  in_10,
  input  in_11,
  input  in_12
);

  wire and_1_out, and_2_out, c_lock_out, clock_1_out, clock_2_out, clock_3_out, d_ff_1_q, d_ff_2_q, d_ff_3_q,
       d_ff_4_q, j_k_ff_1_q, j_k_ff_1_qn, nand_1_out, nand_2_out, nor_1_out, nor_2_out, nor_3_out, nor_4_out,
       not_1_out, t_ff_1_q, t_ff_1_qn;

  Clock clock_1 (.out(clock_1_out));
  Clock c_lock (.out(c_lock_out));
  D_Flip_Flop d_ff_1 (.D(in_9), .clk(clock_1_out), .Q(d_ff_1_q));  // open: Qn, preset, reset
  not not_1 (not_1_out, s_et);
  Clock clock_2 (.out(clock_2_out));
  D_Flip_Flop d_ff_2 (.D(in_10), .clk(clock_1_out), .Q(d_ff_2_q));  // open: Qn, preset, reset
  LED led_1 (.in(d_ff_1_q));
  Clock clock_3 (.out(clock_3_out));
  LED led_2 (.in(d_ff_2_q));
  nor nor_1 (nor_1_out, Set, nor_2_out);
  nor nor_2 (nor_2_out, nor_1_out, Reset);
  nand nand_1 (nand_1_out, S, nand_2_out);
  nand nand_2 (nand_2_out, nand_1_out, Re_set);
  and and_1 (and_1_out, c_lock_out, not_1_out);
  and and_2 (and_2_out, c_lock_out, s_et);
  J_K_Flip_Flop j_k_ff_1 (.J(J), .K(K), .clk(clock_2_out), .Q(j_k_ff_1_q), .Qn(j_k_ff_1_qn));  // open: preset, reset
  T_Flip_Flop t_ff_1 (.T(in_8), .clk(clock_3_out), .Q(t_ff_1_q), .Qn(t_ff_1_qn));  // open: reset, preset
  D_Flip_Flop d_ff_3 (.D(in_11), .clk(clock_1_out), .Q(d_ff_3_q));  // open: Qn, preset, reset
  nor nor_3 (nor_3_out, and_1_out, nor_4_out);
  nor nor_4 (nor_4_out, nor_3_out, and_2_out);
  LED led_3 (.in(j_k_ff_1_q));
  LED led_4 (.in(j_k_ff_1_qn));
  LED led_5 (.in(t_ff_1_q));
  LED led_6 (.in(t_ff_1_qn));
  D_Flip_Flop d_ff_4 (.D(in_12), .clk(clock_1_out), .Q(d_ff_4_q));  // open: Qn, preset, reset
  LED led_7 (.in(d_ff_3_q));
  LED led_8 (.in(nor_1_out));
  LED led_9 (.in(nor_2_out));
  LED led_10 (.in(nand_1_out));
  LED led_11 (.in(nand_2_out));
  LED Q (.in(nor_3_out));
  LED led_12 (.in(d_ff_4_q));
  LED led_13 (.in(nor_4_out));

  // Notes on the sheet:
  //   Q
  //   Q'
  //   Q
  //   Q'
  //   Q
  //   Q'
  //   Q'
endmodule
