// Logisim project Lab04.circ as structural Verilog: 1 circuit, main circuit main
module main (
  input  in_1,
  input  in_2,
  input  in_3,
  input  in_4,
  input  in_5,
  input  in_6,
  input  in_7
);

  wire and_1_out, and_2_out, and_3_out, and_4_out, clock_1_out, clock_2_out, clock_3_out, clock_4_out,
       clock_5_out, j_k_ff_1_q, j_k_ff_3_q, j_k_ff_4_q, j_k_ff_4_qn, j_k_ff_6_q, j_k_ff_7_q, j_k_ff_8_q,
       j_k_ff_8_qn, j_k_ff_10_q, j_k_ff_12_q, j_k_ff_12_qn, j_k_ff_13_q;
  wire [2:0] d_ff_1_q, d_ff_2_q;
  wire [3:0] j_k_ff_2_q, j_k_ff_2_qn, t_ff_1_q, t_ff_1_qn;

  Clock clock_1 (.out(clock_1_out));
  Clock clock_2 (.out(clock_2_out));
  Clock clock_3 (.out(clock_3_out));
  Clock clock_4 (.out(clock_4_out));
  Clock clock_5 (.out(clock_5_out));
  J_K_Flip_Flop #(.trigger("falling")) j_k_ff_1 (
    .J(in_6), .K(in_6), .clk(clock_1_out), .Q(j_k_ff_1_q), .reset(and_4_out));  // open: Qn, preset
  J_K_Flip_Flop #(.trigger("falling")) j_k_ff_2 (
    .J(in_1), .K(in_1), .clk(clock_2_out), .Q(j_k_ff_2_q[0]), .Qn(j_k_ff_2_qn[0]));  // open: preset, reset
  T_Flip_Flop t_ff_1 (.T(in_2), .clk(clock_3_out), .Q(t_ff_1_q[0]), .Qn(t_ff_1_qn[0]));  // open: reset, preset
  J_K_Flip_Flop #(.trigger("falling")) j_k_ff_3 (
    .J(in_3), .K(in_3), .clk(clock_4_out), .Q(j_k_ff_3_q), .reset(and_3_out));  // open: Qn, preset
  J_K_Flip_Flop #(.trigger("falling")) j_k_ff_4 (
    .J(in_5), .K(in_5), .clk(clock_5_out), .Q(j_k_ff_4_q), .Qn(j_k_ff_4_qn));  // open: preset, reset
  J_K_Flip_Flop #(.trigger("falling")) j_k_ff_5 (
    .J(in_1), .K(in_1), .clk(j_k_ff_2_q[0]), .Q(j_k_ff_2_q[1]), .Qn(j_k_ff_2_qn[1]));  // open: preset, reset
  LED led_1 (.in(j_k_ff_2_q[0]));
  LED led_2 (.in(j_k_ff_2_qn[0]));
  T_Flip_Flop t_ff_2 (.T(in_2), .clk(t_ff_1_q[0]), .Q(t_ff_1_q[1]), .Qn(t_ff_1_qn[1]));  // open: reset, preset
  LED led_3 (.in(t_ff_1_q[0]));
  LED led_4 (.in(t_ff_1_qn[0]));
  LED led_5 (.in(j_k_ff_4_q));
  LED led_6 (.in(j_k_ff_4_qn));
  J_K_Flip_Flop #(.trigger("falling")) j_k_ff_6 (
    .J(j_k_ff_1_q), .K(j_k_ff_1_q), .clk(clock_1_out), .Q(j_k_ff_6_q), .reset(and_4_out));  // open: Qn, preset
  D_Flip_Flop d_ff_1 (.D(j_k_ff_1_q), .clk(clock_1_out), .Q(d_ff_1_q[0]));  // open: Qn, preset, reset
  LED led_7 (.in(j_k_ff_2_q[1]));
  LED led_8 (.in(j_k_ff_2_qn[1]));
  LED led_9 (.in(t_ff_1_qn[1]));
  J_K_Flip_Flop #(.trigger("falling")) j_k_ff_7 (
    .J(j_k_ff_3_q), .K(j_k_ff_3_q), .clk(clock_4_out), .Q(j_k_ff_7_q), .reset(and_3_out));  // open: Qn, preset
  D_Flip_Flop d_ff_2 (.D(j_k_ff_3_q), .clk(clock_4_out), .Q(d_ff_2_q[0]));  // open: Qn, preset, reset
  LED led_10 (.in(d_ff_2_q[0]));
  J_K_Flip_Flop #(.trigger("falling")) j_k_ff_8 (
    .J(in_5), .K(in_5), .clk(j_k_ff_4_q), .Q(j_k_ff_8_q), .Qn(j_k_ff_8_qn));  // open: preset, reset
  LED led_11 (.in(d_ff_1_q[0]));
  J_K_Flip_Flop #(.trigger("falling")) j_k_ff_9 (
    .J(in_1), .K(in_1), .clk(j_k_ff_2_q[1]), .Q(j_k_ff_2_q[2]), .Qn(j_k_ff_2_qn[2]));  // open: preset, reset
  LED led_12 (.in(j_k_ff_2_qn[2]));
  T_Flip_Flop t_ff_3 (.T(in_2), .clk(t_ff_1_q[1]), .Q(t_ff_1_q[2]), .Qn(t_ff_1_qn[2]));  // open: reset, preset
  LED led_13 (.in(t_ff_1_q[1]));
  J_K_Flip_Flop #(.trigger("falling")) j_k_ff_10 (
    .J(and_2_out), .K(and_2_out), .clk(clock_4_out), .Q(j_k_ff_10_q), .reset(and_3_out));  // open: Qn, preset
  D_Flip_Flop d_ff_3 (.D(j_k_ff_7_q), .clk(clock_4_out), .Q(d_ff_2_q[1]));  // open: Qn, preset, reset
  LED led_14 (.in(j_k_ff_8_q));
  LED led_15 (.in(j_k_ff_8_qn));
  and and_1 (and_1_out, j_k_ff_1_q, j_k_ff_6_q);
  D_Flip_Flop d_ff_4 (.D(j_k_ff_6_q), .clk(clock_1_out), .Q(d_ff_1_q[1]));  // open: Qn, preset, reset
  J_K_Flip_Flop #(.trigger("falling")) j_k_ff_11 (
    .J(in_1), .K(in_1), .clk(j_k_ff_2_q[2]), .Q(j_k_ff_2_q[3]), .Qn(j_k_ff_2_qn[3]));  // open: preset, reset
  LED led_16 (.in(j_k_ff_2_q[2]));
  LED led_17 (.in(t_ff_1_q[2]));
  LED led_18 (.in(t_ff_1_qn[2]));
  and and_2 (and_2_out, j_k_ff_3_q, j_k_ff_7_q);
  LED led_19 (.in(d_ff_2_q[1]));
  J_K_Flip_Flop #(.trigger("falling")) j_k_ff_12 (
    .J(in_5), .K(in_5), .clk(j_k_ff_8_q), .Q(j_k_ff_12_q), .Qn(j_k_ff_12_qn));  // open: preset, reset
  LED led_20 (.in(j_k_ff_12_qn));
  J_K_Flip_Flop #(.trigger("falling")) j_k_ff_13 (
    .J(and_1_out), .K(and_1_out), .clk(clock_1_out), .Q(j_k_ff_13_q), .reset(and_4_out));  // open: Qn, preset
  LED led_21 (.in(d_ff_1_q[1]));
  LED led_22 (.in(j_k_ff_2_q[3]));
  LED led_23 (.in(j_k_ff_2_qn[3]));
  T_Flip_Flop t_ff_4 (.T(in_2), .clk(t_ff_1_q[2]), .Q(t_ff_1_q[3]), .Qn(t_ff_1_qn[3]));  // open: reset, preset
  LED led_24 (.in(t_ff_1_qn[3]));
  and and_3 (and_3_out, j_k_ff_10_q, j_k_ff_3_q);
  D_Flip_Flop d_ff_5 (.D(j_k_ff_10_q), .clk(clock_4_out), .Q(d_ff_2_q[2]));  // open: Qn, preset, reset
  LED led_25 (.in(j_k_ff_12_q));
  and and_4 (and_4_out, j_k_ff_13_q, j_k_ff_6_q);
  D_Flip_Flop d_ff_6 (.D(j_k_ff_13_q), .clk(clock_1_out), .Q(d_ff_1_q[2]));  // open: Qn, preset, reset
  LED led_26 (.in(t_ff_1_q[3]));
  LED led_27 (.in(d_ff_2_q[2]));
  Hex_Digit_Display hex_digit_display_1 (.value(j_k_ff_2_q));  // open: dp
  Hex_Digit_Display hex_digit_display_2 (.value(t_ff_1_q));  // open: dp
  Hex_Digit_Display hex_digit_display_3 (.value(t_ff_1_qn));  // open: dp
  LED led_28 (.in(d_ff_1_q[2]));
  Hex_Digit_Display hex_digit_display_4 (.value(j_k_ff_2_qn));  // open: dp
  Hex_Digit_Display hex_digit_display_5 (.value({in_4, d_ff_2_q}));  // open: dp
  Hex_Digit_Display hex_digit_display_6 (.value({in_7, d_ff_1_q}));  // open: dp
endmodule
